// Logisim project projectB.circ as structural Verilog: 21 circuits, main circuit videocarta
module main (
);

  wire \_1_2_выбор , _1_2p, keyboard_1_avail, not_1_out, not_2_out, score_1_restart, \меню_игра ,
       \рядом_слева , \рядом_справа ;
  wire [3:0] borders_1_bus_0, borders_1_bus_0_2, borders_1_bus_0_3, borders_1_bus_0_4, borders_1_bus_0_5,
       borders_1_bus_0_6, borders_1_bus_0_7, borders_1_bus_0_8, borders_1_bus_0_9, borders_1_bus_0_10,
       borders_1_bus_0_11, borders_1_bus_0_12, borders_1_bus_0_13, borders_1_bus_0_14, borders_1_bus_0_15,
       borders_1_bus_0_16, borders_1_bus_0_17, borders_1_bus_0_18, borders_1_bus_0_19, borders_1_bus_0_20,
       borders_1_bus_0_21, borders_1_bus_0_22, borders_1_bus_0_23, borders_1_bus_0_24, borders_1_bus_0_25,
       borders_1_bus_0_26, borders_1_bus_0_27, borders_1_bus_0_28, borders_1_bus_0_29, borders_1_bus_0_30,
       borders_1_bus_0_31, borders_1_bus_0_32, borders_1_bus_0_33, borders_1_bus_0_34, borders_1_bus_0_35,
       borders_1_bus_0_36, borders_1_bus_0_37, borders_1_bus_0_38, borders_1_bus_0_39, borders_1_bus_0_40,
       borders_1_bus_0_41, borders_1_bus_0_42, borders_1_bus_0_43, borders_1_bus_0_44, borders_1_bus_0_45,
       borders_1_bus_0_46, borders_1_bus_0_47, borders_1_bus_0_48, borders_1_bus_0_49, borders_1_bus_0_50,
       borders_1_bus_0_51, borders_1_bus_0_52, borders_1_bus_0_53, borders_1_bus_0_54, borders_1_bus_0_55,
       borders_1_bus_0_56, borders_1_bus_0_57, borders_1_bus_0_58, borders_1_bus_0_59, borders_1_bus_0_60,
       borders_1_bus_0_61, borders_1_bus_0_62, borders_1_bus_0_63, borders_1_bus_0_64, borders_1_bus_0_65,
       borders_1_bus_0_66, borders_1_bus_0_67, borders_1_bus_0_68, borders_1_bus_0_69, borders_1_bus_0_70,
       borders_1_bus_0_71, borders_1_bus_0_72, borders_1_bus_0_73, borders_1_bus_0_74, borders_1_bus_0_75,
       borders_1_bus_0_76, borders_1_bus_0_77, borders_1_bus_0_78, borders_1_bus_0_79, borders_1_bus_0_80,
       borders_1_bus_0_81, borders_1_bus_0_82, borders_1_bus_0_83, borders_1_bus_0_84, borders_1_bus_0_85,
       borders_1_bus_0_86, borders_1_bus_0_87, borders_1_bus_0_88, borders_1_bus_0_89, borders_1_bus_0_90,
       borders_1_bus_0_91, borders_1_bus_0_92, borders_1_bus_0_93, borders_1_bus_0_94, borders_1_bus_0_95,
       borders_1_bus_0_96, borders_1_bus_0_97, borders_1_bus_0_98, borders_1_bus_0_99, borders_1_bus_0_100,
       borders_1_bus_0_101, borders_1_bus_0_102, borders_1_bus_0_103, borders_1_bus_0_104,
       borders_1_bus_0_105, borders_1_bus_0_106, borders_1_bus_0_107, borders_1_bus_0_108,
       borders_1_bus_0_109, borders_1_bus_0_110, borders_1_bus_0_111, borders_1_bus_0_112,
       borders_1_bus_0_113, borders_1_bus_0_114, borders_1_bus_0_115, borders_1_bus_0_116,
       borders_1_bus_0_117, borders_1_bus_0_118, borders_1_bus_0_119, borders_1_bus_0_120,
       borders_1_bus_0_121, borders_1_bus_0_122, borders_1_bus_0_123, borders_1_bus_0_124,
       borders_1_bus_0_125, borders_1_bus_0_126, borders_1_bus_0_127, borders_1_bus_0_128,
       borders_1_bus_0_129, borders_1_bus_0_130, borders_1_bus_0_131, borders_1_bus_0_132,
       borders_1_bus_0_133, borders_1_bus_0_134, borders_1_bus_0_135, borders_1_bus_0_136,
       borders_1_bus_0_137, borders_1_bus_0_138, borders_1_bus_0_139, borders_1_bus_0_140,
       borders_1_bus_0_141, borders_1_bus_0_142, borders_1_bus_0_143, borders_1_bus_0_144,
       borders_1_bus_0_145, borders_1_bus_0_146, borders_1_bus_0_147, borders_1_bus_0_148,
       borders_1_bus_0_149, borders_1_bus_0_150, borders_1_bus_0_151, borders_1_bus_0_152,
       borders_1_bus_0_153, borders_1_bus_0_154, borders_1_bus_0_155, borders_1_bus_0_156,
       borders_1_bus_0_157, borders_1_bus_0_158, borders_1_bus_0_159, borders_1_bus_0_160,
       borders_1_bus_0_161, borders_1_bus_0_162, borders_1_bus_0_163, borders_1_bus_0_164,
       borders_1_bus_0_165, borders_1_bus_0_166, borders_1_bus_0_167, borders_1_bus_0_168,
       borders_1_bus_0_169, borders_1_bus_0_170, borders_1_bus_0_171, borders_1_bus_0_172,
       borders_1_bus_0_173, borders_1_bus_0_174, borders_1_bus_0_175, borders_1_bus_0_176,
       borders_1_bus_0_177, borders_1_bus_0_178, borders_1_bus_0_179, borders_1_bus_0_180,
       borders_1_bus_0_181, borders_1_bus_0_182, borders_1_bus_0_183, borders_1_bus_0_184,
       borders_1_bus_0_185, borders_1_bus_0_186, borders_1_bus_0_187, borders_1_bus_0_188,
       borders_1_bus_0_189, borders_1_bus_0_190, borders_1_bus_0_191, borders_1_bus_0_192,
       borders_1_bus_0_193, borders_1_bus_0_194, borders_1_bus_0_195, borders_1_bus_0_196,
       borders_1_bus_0_197, borders_1_bus_0_198, borders_1_bus_0_199, borders_1_bus_0_200,
       borders_1_bus_0_201, borders_1_bus_0_202, borders_1_bus_0_203, borders_1_bus_0_204,
       borders_1_bus_0_205, borders_1_bus_0_206, borders_1_bus_0_207, borders_1_bus_0_208, \слева_десятки ,
       \слева_единицы , \справа_десятки , \справа_единицы ;
  wire [6:0] keyboard_1_data;
  wire [31:0] lbat, rbat, videocarta_1_out_8, videocarta_1_out_9, videocarta_1_out_10, videocarta_1_out_11,
       videocarta_1_out_12, videocarta_1_out_13, videocarta_1_out_14, videocarta_1_out_15,
       videocarta_1_out_16, videocarta_1_out_17, videocarta_1_out_18, videocarta_1_out_19,
       videocarta_1_out_20, videocarta_1_out_21, videocarta_1_out_22, videocarta_1_out_23,
       videocarta_1_out_24, videocarta_1_out_25, videocarta_1_out_26, videocarta_1_out_27,
       videocarta_1_out_28, videocarta_1_out_29, videocarta_1_out_30, videocarta_1_out_31,
       videocarta_1_out_32, videocarta_1_out_33, videocarta_1_out_34, videocarta_1_out_35,
       videocarta_1_out_36, videocarta_1_out_37, videocarta_1_out_38, videocarta_1_out_39,
       videocarta_1_out_40, videocarta_1_out_41, videocarta_1_out_42, videocarta_1_out_43,
       videocarta_1_out_44, videocarta_1_out_45, videocarta_1_out_46, videocarta_1_out_47,
       videocarta_1_out_48, videocarta_1_out_49, videocarta_1_out_50, videocarta_1_out_51,
       videocarta_1_out_52, videocarta_1_out_53, videocarta_1_out_54, videocarta_1_out_55,
       videocarta_1_out_56, videocarta_1_out_57, videocarta_1_out_58, videocarta_1_out_59,
       videocarta_1_out_60, videocarta_1_out_61, videocarta_1_out_62, videocarta_1_out_63,
       videocarta_1_out_64, videocarta_1_out_65, videocarta_1_out_66, videocarta_1_out_67,
       videocarta_1_out_68, videocarta_1_out_69, videocarta_1_out_70, videocarta_1_out_71, x1, x2, y;

  Hex_Digit_Display hex_digit_display_1 (.value(\слева_единицы ));  // open: dp
  Hex_Digit_Display hex_digit_display_2 (.value(\слева_десятки ));  // open: dp
  borders borders_1 (
    .\меню_игра (\меню_игра ), .bus_0(borders_1_bus_0), .bus_0_19(borders_1_bus_0_19),
    .bus_0_37(borders_1_bus_0_37), .bus_0_55(borders_1_bus_0_55), .bus_0_2(borders_1_bus_0_2),
    .bus_0_20(borders_1_bus_0_20), .bus_0_38(borders_1_bus_0_38), .bus_0_56(borders_1_bus_0_56),
    .bus_0_3(borders_1_bus_0_3), .bus_0_21(borders_1_bus_0_21), .bus_0_39(borders_1_bus_0_39),
    .bus_0_57(borders_1_bus_0_57), .bus_0_4(borders_1_bus_0_4), .bus_0_22(borders_1_bus_0_22),
    .bus_0_40(borders_1_bus_0_40), .bus_0_58(borders_1_bus_0_58), .bus_0_5(borders_1_bus_0_5),
    .bus_0_23(borders_1_bus_0_23), .bus_0_41(borders_1_bus_0_41), .bus_0_59(borders_1_bus_0_59),
    .bus_0_6(borders_1_bus_0_6), .bus_0_24(borders_1_bus_0_24), .bus_0_42(borders_1_bus_0_42),
    .bus_0_60(borders_1_bus_0_60), .bus_0_7(borders_1_bus_0_7), .bus_0_25(borders_1_bus_0_25),
    .bus_0_43(borders_1_bus_0_43), .bus_0_61(borders_1_bus_0_61), .bus_0_8(borders_1_bus_0_8),
    .bus_0_26(borders_1_bus_0_26), .bus_0_44(borders_1_bus_0_44), .bus_0_62(borders_1_bus_0_62),
    .bus_0_9(borders_1_bus_0_9), .bus_0_27(borders_1_bus_0_27), .bus_0_45(borders_1_bus_0_45),
    .bus_0_63(borders_1_bus_0_63), .bus_0_10(borders_1_bus_0_10), .bus_0_28(borders_1_bus_0_28),
    .bus_0_46(borders_1_bus_0_46), .bus_0_64(borders_1_bus_0_64), .bus_0_11(borders_1_bus_0_11),
    .bus_0_29(borders_1_bus_0_29), .bus_0_47(borders_1_bus_0_47), .bus_0_65(borders_1_bus_0_65),
    .bus_0_12(borders_1_bus_0_12), .bus_0_30(borders_1_bus_0_30), .bus_0_48(borders_1_bus_0_48),
    .bus_0_66(borders_1_bus_0_66), .bus_0_13(borders_1_bus_0_13), .bus_0_31(borders_1_bus_0_31),
    .bus_0_49(borders_1_bus_0_49), .bus_0_67(borders_1_bus_0_67), .bus_0_14(borders_1_bus_0_14),
    .bus_0_32(borders_1_bus_0_32), .bus_0_50(borders_1_bus_0_50), .bus_0_68(borders_1_bus_0_68),
    .bus_0_15(borders_1_bus_0_15), .bus_0_33(borders_1_bus_0_33), .bus_0_51(borders_1_bus_0_51),
    .bus_0_69(borders_1_bus_0_69), .bus_0_16(borders_1_bus_0_16), .bus_0_34(borders_1_bus_0_34),
    .bus_0_52(borders_1_bus_0_52), .bus_0_70(borders_1_bus_0_70), .bus_0_17(borders_1_bus_0_17),
    .bus_0_35(borders_1_bus_0_35), .bus_0_53(borders_1_bus_0_53), .bus_0_71(borders_1_bus_0_71),
    .bus_0_18(borders_1_bus_0_18), .bus_0_36(borders_1_bus_0_36), .bus_0_54(borders_1_bus_0_54),
    .bus_0_72(borders_1_bus_0_72), .bus_0_73(borders_1_bus_0_73), .bus_0_75(borders_1_bus_0_75),
    .bus_0_77(borders_1_bus_0_77), .bus_0_79(borders_1_bus_0_79), .bus_0_81(borders_1_bus_0_81),
    .bus_0_83(borders_1_bus_0_83), .bus_0_85(borders_1_bus_0_85), .bus_0_87(borders_1_bus_0_87),
    .bus_0_89(borders_1_bus_0_89), .bus_0_91(borders_1_bus_0_91), .bus_0_93(borders_1_bus_0_93),
    .bus_0_95(borders_1_bus_0_95), .bus_0_97(borders_1_bus_0_97), .bus_0_99(borders_1_bus_0_99),
    .bus_0_101(borders_1_bus_0_101), .bus_0_103(borders_1_bus_0_103), .bus_0_105(borders_1_bus_0_105),
    .bus_0_113(borders_1_bus_0_113), .bus_0_121(borders_1_bus_0_121), .bus_0_107(borders_1_bus_0_107),
    .bus_0_115(borders_1_bus_0_115), .bus_0_123(borders_1_bus_0_123), .bus_0_109(borders_1_bus_0_109),
    .bus_0_117(borders_1_bus_0_117), .bus_0_125(borders_1_bus_0_125), .bus_0_111(borders_1_bus_0_111),
    .bus_0_119(borders_1_bus_0_119), .bus_0_127(borders_1_bus_0_127), .bus_0_129(borders_1_bus_0_129),
    .bus_0_131(borders_1_bus_0_131), .bus_0_133(borders_1_bus_0_133), .bus_0_135(borders_1_bus_0_135),
    .bus_0_76(borders_1_bus_0_76), .bus_0_78(borders_1_bus_0_78), .bus_0_80(borders_1_bus_0_80),
    .bus_0_74(borders_1_bus_0_74), .bus_0_82(borders_1_bus_0_82), .bus_0_84(borders_1_bus_0_84),
    .bus_0_86(borders_1_bus_0_86), .bus_0_88(borders_1_bus_0_88), .bus_0_90(borders_1_bus_0_90),
    .bus_0_92(borders_1_bus_0_92), .bus_0_94(borders_1_bus_0_94), .bus_0_96(borders_1_bus_0_96),
    .bus_0_98(borders_1_bus_0_98), .bus_0_100(borders_1_bus_0_100), .bus_0_102(borders_1_bus_0_102),
    .bus_0_104(borders_1_bus_0_104), .bus_0_106(borders_1_bus_0_106), .bus_0_108(borders_1_bus_0_108),
    .bus_0_110(borders_1_bus_0_110), .bus_0_112(borders_1_bus_0_112), .bus_0_114(borders_1_bus_0_114),
    .bus_0_122(borders_1_bus_0_122), .bus_0_116(borders_1_bus_0_116), .bus_0_124(borders_1_bus_0_124),
    .bus_0_126(borders_1_bus_0_126), .bus_0_120(borders_1_bus_0_120), .bus_0_128(borders_1_bus_0_128),
    .bus_0_130(borders_1_bus_0_130), .bus_0_132(borders_1_bus_0_132), .bus_0_134(borders_1_bus_0_134),
    .bus_0_136(borders_1_bus_0_136), .bus_0_118(borders_1_bus_0_118), .bus_0_137(borders_1_bus_0_137),
    .bus_0_155(borders_1_bus_0_155), .bus_0_173(borders_1_bus_0_173), .bus_0_191(borders_1_bus_0_191),
    .bus_0_138(borders_1_bus_0_138), .bus_0_156(borders_1_bus_0_156), .bus_0_174(borders_1_bus_0_174),
    .bus_0_192(borders_1_bus_0_192), .bus_0_139(borders_1_bus_0_139), .bus_0_157(borders_1_bus_0_157),
    .bus_0_175(borders_1_bus_0_175), .bus_0_193(borders_1_bus_0_193), .bus_0_140(borders_1_bus_0_140),
    .bus_0_158(borders_1_bus_0_158), .bus_0_176(borders_1_bus_0_176), .bus_0_194(borders_1_bus_0_194),
    .bus_0_141(borders_1_bus_0_141), .bus_0_159(borders_1_bus_0_159), .bus_0_177(borders_1_bus_0_177),
    .bus_0_195(borders_1_bus_0_195), .bus_0_142(borders_1_bus_0_142), .bus_0_160(borders_1_bus_0_160),
    .bus_0_178(borders_1_bus_0_178), .bus_0_196(borders_1_bus_0_196), .bus_0_143(borders_1_bus_0_143),
    .bus_0_161(borders_1_bus_0_161), .bus_0_179(borders_1_bus_0_179), .bus_0_197(borders_1_bus_0_197),
    .bus_0_144(borders_1_bus_0_144), .bus_0_162(borders_1_bus_0_162), .bus_0_180(borders_1_bus_0_180),
    .bus_0_198(borders_1_bus_0_198), .bus_0_145(borders_1_bus_0_145), .bus_0_163(borders_1_bus_0_163),
    .bus_0_181(borders_1_bus_0_181), .bus_0_199(borders_1_bus_0_199), .bus_0_146(borders_1_bus_0_146),
    .bus_0_147(borders_1_bus_0_147), .bus_0_148(borders_1_bus_0_148), .bus_0_149(borders_1_bus_0_149),
    .bus_0_150(borders_1_bus_0_150), .bus_0_151(borders_1_bus_0_151), .bus_0_152(borders_1_bus_0_152),
    .bus_0_153(borders_1_bus_0_153), .bus_0_164(borders_1_bus_0_164), .bus_0_165(borders_1_bus_0_165),
    .bus_0_166(borders_1_bus_0_166), .bus_0_167(borders_1_bus_0_167), .bus_0_168(borders_1_bus_0_168),
    .bus_0_169(borders_1_bus_0_169), .bus_0_170(borders_1_bus_0_170), .bus_0_171(borders_1_bus_0_171),
    .bus_0_182(borders_1_bus_0_182), .bus_0_183(borders_1_bus_0_183), .bus_0_184(borders_1_bus_0_184),
    .bus_0_185(borders_1_bus_0_185), .bus_0_186(borders_1_bus_0_186), .bus_0_187(borders_1_bus_0_187),
    .bus_0_188(borders_1_bus_0_188), .bus_0_189(borders_1_bus_0_189), .bus_0_200(borders_1_bus_0_200),
    .bus_0_202(borders_1_bus_0_202), .bus_0_203(borders_1_bus_0_203), .bus_0_204(borders_1_bus_0_204),
    .bus_0_205(borders_1_bus_0_205), .bus_0_206(borders_1_bus_0_206), .bus_0_207(borders_1_bus_0_207),
    .bus_0_201(borders_1_bus_0_201), .bus_0_154(borders_1_bus_0_154), .bus_0_172(borders_1_bus_0_172),
    .bus_0_190(borders_1_bus_0_190), .bus_0_208(borders_1_bus_0_208));
  DotMatrix #(.matrixcols(4), .matrixrows(4)) dotmatrix_1 (
    .col0(borders_1_bus_0), .col1(borders_1_bus_0_19), .col2(borders_1_bus_0_37), .col3(borders_1_bus_0_55));
  DotMatrix #(.matrixcols(4), .matrixrows(4)) dotmatrix_2 (
    .col0(borders_1_bus_0_73), .col1(borders_1_bus_0_75), .col2(borders_1_bus_0_77), .col3(borders_1_bus_0_79));
  DotMatrix #(.matrixcols(4), .matrixrows(4)) dotmatrix_3 (
    .col0(borders_1_bus_0_81), .col1(borders_1_bus_0_83), .col2(borders_1_bus_0_85), .col3(borders_1_bus_0_87));
  DotMatrix #(.matrixcols(4), .matrixrows(4)) dotmatrix_4 (
    .col0(borders_1_bus_0_89), .col1(borders_1_bus_0_91), .col2(borders_1_bus_0_93), .col3(borders_1_bus_0_95));
  DotMatrix #(.matrixcols(4), .matrixrows(4)) dotmatrix_5 (
    .col0(borders_1_bus_0_97), .col1(borders_1_bus_0_99), .col2(borders_1_bus_0_101),
    .col3(borders_1_bus_0_103));
  DotMatrix #(.matrixcols(4), .matrixrows(4)) dotmatrix_6 (
    .col0(borders_1_bus_0_105), .col1(borders_1_bus_0_107), .col2(borders_1_bus_0_109),
    .col3(borders_1_bus_0_111));
  DotMatrix #(.matrixcols(4), .matrixrows(4)) dotmatrix_7 (
    .col0(borders_1_bus_0_113), .col1(borders_1_bus_0_115), .col2(borders_1_bus_0_117),
    .col3(borders_1_bus_0_119));
  DotMatrix #(.matrixcols(4), .matrixrows(4)) dotmatrix_8 (
    .col0(borders_1_bus_0_121), .col1(borders_1_bus_0_123), .col2(borders_1_bus_0_125),
    .col3(borders_1_bus_0_127));
  DotMatrix #(.matrixcols(4), .matrixrows(4)) dotmatrix_9 (
    .col0(borders_1_bus_0_129), .col1(borders_1_bus_0_131), .col2(borders_1_bus_0_133),
    .col3(borders_1_bus_0_135));
  DotMatrix #(.matrixcols(4), .matrixrows(4)) dotmatrix_10 (
    .col0(borders_1_bus_0_137), .col1(borders_1_bus_0_155), .col2(borders_1_bus_0_173),
    .col3(borders_1_bus_0_191));
  DotMatrix #(.matrixcols(4), .matrixrows(4)) dotmatrix_11 (
    .col0(borders_1_bus_0_3), .col1(borders_1_bus_0_21), .col2(borders_1_bus_0_39), .col3(borders_1_bus_0_57));
  DotMatrix #(.matrixcols(4), .matrixrows(4)) dotmatrix_12 (
    .col0(borders_1_bus_0_2), .col1(borders_1_bus_0_20), .col2(borders_1_bus_0_38), .col3(borders_1_bus_0_56));
  DotMatrix #(.matrixcols(32), .matrixrows(32)) dotmatrix_13 (
    .col0(videocarta_1_out_8), .col1(videocarta_1_out_9), .col2(videocarta_1_out_10),
    .col3(videocarta_1_out_12), .col4(videocarta_1_out_14), .col5(videocarta_1_out_16),
    .col6(videocarta_1_out_18), .col7(videocarta_1_out_20), .col8(videocarta_1_out_22),
    .col9(videocarta_1_out_24), .col10(videocarta_1_out_26), .col11(videocarta_1_out_28),
    .col12(videocarta_1_out_30), .col13(videocarta_1_out_32), .col14(videocarta_1_out_34),
    .col15(videocarta_1_out_36), .col16(videocarta_1_out_11), .col17(videocarta_1_out_13),
    .col18(videocarta_1_out_15), .col19(videocarta_1_out_17), .col20(videocarta_1_out_19),
    .col21(videocarta_1_out_21), .col22(videocarta_1_out_23), .col23(videocarta_1_out_25),
    .col24(videocarta_1_out_27), .col25(videocarta_1_out_29), .col26(videocarta_1_out_31),
    .col27(videocarta_1_out_33), .col28(videocarta_1_out_35), .col29(videocarta_1_out_37),
    .col30(videocarta_1_out_38), .col31(videocarta_1_out_39));
  videocarta videocarta_1 (
    .y(y), .x(x1), .out_11(videocarta_1_out_11), .out_8(videocarta_1_out_8), .out_13(videocarta_1_out_13),
    .out_15(videocarta_1_out_15), .out_10(videocarta_1_out_10), .out_9(videocarta_1_out_9),
    .out_17(videocarta_1_out_17), .out_12(videocarta_1_out_12), .out_19(videocarta_1_out_19),
    .out_14(videocarta_1_out_14), .out_21(videocarta_1_out_21), .out_16(videocarta_1_out_16),
    .out_18(videocarta_1_out_18), .out_23(videocarta_1_out_23), .out_25(videocarta_1_out_25),
    .out_20(videocarta_1_out_20), .out_27(videocarta_1_out_27), .out_22(videocarta_1_out_22),
    .out_29(videocarta_1_out_29), .out_31(videocarta_1_out_31), .out_24(videocarta_1_out_24),
    .out_26(videocarta_1_out_26), .out_33(videocarta_1_out_33), .out_28(videocarta_1_out_28),
    .out_35(videocarta_1_out_35), .out_37(videocarta_1_out_37), .out_30(videocarta_1_out_30),
    .out_32(videocarta_1_out_32), .out_38(videocarta_1_out_38), .out_34(videocarta_1_out_34),
    .out_36(videocarta_1_out_36), .out_71(videocarta_1_out_71), .palka_left(lbat), .palka_right(rbat),
    .out_43(videocarta_1_out_43), .out_40(videocarta_1_out_40), .out_45(videocarta_1_out_45),
    .out_41(videocarta_1_out_41), .out_47(videocarta_1_out_47), .out_42(videocarta_1_out_42),
    .out_49(videocarta_1_out_49), .out_44(videocarta_1_out_44), .out_51(videocarta_1_out_51),
    .out_46(videocarta_1_out_46), .out_53(videocarta_1_out_53), .out_48(videocarta_1_out_48),
    .out_55(videocarta_1_out_55), .out_50(videocarta_1_out_50), .out_57(videocarta_1_out_57),
    .out_52(videocarta_1_out_52), .out_59(videocarta_1_out_59), .out_54(videocarta_1_out_54),
    .out_61(videocarta_1_out_61), .out_56(videocarta_1_out_56), .out_63(videocarta_1_out_63),
    .out_58(videocarta_1_out_58), .out_65(videocarta_1_out_65), .out_60(videocarta_1_out_60),
    .out_67(videocarta_1_out_67), .out_62(videocarta_1_out_62), .out_69(videocarta_1_out_69),
    .out_64(videocarta_1_out_64), .out_70(videocarta_1_out_70), .out_66(videocarta_1_out_66), .x2(x2),
    .out_39(videocarta_1_out_39), .out_68(videocarta_1_out_68), .\меню_игра (\меню_игра ),
    ._1_2_p(\_1_2_выбор ));
  DotMatrix #(.matrixcols(4), .matrixrows(4)) dotmatrix_14 (
    .col0(borders_1_bus_0_138), .col1(borders_1_bus_0_156), .col2(borders_1_bus_0_174),
    .col3(borders_1_bus_0_192));
  DotMatrix #(.matrixcols(4), .matrixrows(4)) dotmatrix_15 (
    .col0(borders_1_bus_0_139), .col1(borders_1_bus_0_157), .col2(borders_1_bus_0_175),
    .col3(borders_1_bus_0_193));
  DotMatrix #(.matrixcols(4), .matrixrows(4)) dotmatrix_16 (
    .col0(borders_1_bus_0_4), .col1(borders_1_bus_0_22), .col2(borders_1_bus_0_40), .col3(borders_1_bus_0_58));
  DotMatrix #(.matrixcols(4), .matrixrows(4)) dotmatrix_17 (
    .col0(borders_1_bus_0_5), .col1(borders_1_bus_0_23), .col2(borders_1_bus_0_41), .col3(borders_1_bus_0_59));
  DotMatrix #(.matrixcols(4), .matrixrows(4)) dotmatrix_18 (
    .col0(borders_1_bus_0_140), .col1(borders_1_bus_0_158), .col2(borders_1_bus_0_176),
    .col3(borders_1_bus_0_194));
  DotMatrix #(.matrixcols(4), .matrixrows(4)) dotmatrix_19 (
    .col0(borders_1_bus_0_141), .col1(borders_1_bus_0_159), .col2(borders_1_bus_0_177),
    .col3(borders_1_bus_0_195));
  Keyboard keyboard_1 (.clk(not_1_out), .re(1'b1), .clr(1'b0), .avail(keyboard_1_avail), .data(keyboard_1_data));
  not not_1 (not_1_out, not_2_out);
  DotMatrix #(.matrixcols(4), .matrixrows(4)) dotmatrix_20 (
    .col0(borders_1_bus_0_7), .col1(borders_1_bus_0_25), .col2(borders_1_bus_0_43), .col3(borders_1_bus_0_61));
  DotMatrix #(.matrixcols(4), .matrixrows(4)) dotmatrix_21 (
    .col0(borders_1_bus_0_6), .col1(borders_1_bus_0_24), .col2(borders_1_bus_0_42), .col3(borders_1_bus_0_60));
  DotMatrix #(.matrixcols(4), .matrixrows(4)) dotmatrix_22 (
    .col0(borders_1_bus_0_142), .col1(borders_1_bus_0_160), .col2(borders_1_bus_0_178),
    .col3(borders_1_bus_0_196));
  DotMatrix #(.matrixcols(4), .matrixrows(4)) dotmatrix_23 (
    .col0(borders_1_bus_0_143), .col1(borders_1_bus_0_161), .col2(borders_1_bus_0_179),
    .col3(borders_1_bus_0_197));
  not not_2 (not_2_out, keyboard_1_avail);
  DotMatrix #(.matrixcols(4), .matrixrows(4)) dotmatrix_24 (
    .col0(borders_1_bus_0_8), .col1(borders_1_bus_0_26), .col2(borders_1_bus_0_44), .col3(borders_1_bus_0_62));
  DotMatrix #(.matrixcols(4), .matrixrows(4)) dotmatrix_25 (
    .col0(borders_1_bus_0_9), .col1(borders_1_bus_0_27), .col2(borders_1_bus_0_45), .col3(borders_1_bus_0_63));
  DotMatrix #(.matrixcols(4), .matrixrows(4)) dotmatrix_26 (
    .col0(borders_1_bus_0_145), .col1(borders_1_bus_0_163), .col2(borders_1_bus_0_181),
    .col3(borders_1_bus_0_199));
  DotMatrix #(.matrixcols(4), .matrixrows(4)) dotmatrix_27 (
    .col0(borders_1_bus_0_144), .col1(borders_1_bus_0_162), .col2(borders_1_bus_0_180),
    .col3(borders_1_bus_0_198));
  DotMatrix #(.matrixcols(4), .matrixrows(4)) dotmatrix_28 (
    .col0(borders_1_bus_0_10), .col1(borders_1_bus_0_28), .col2(borders_1_bus_0_46), .col3(borders_1_bus_0_64));
  DotMatrix #(.matrixcols(4), .matrixrows(4)) dotmatrix_29 (
    .col0(borders_1_bus_0_11), .col1(borders_1_bus_0_29), .col2(borders_1_bus_0_47), .col3(borders_1_bus_0_65));
  DotMatrix #(.matrixcols(32), .matrixrows(32)) dotmatrix_30 (
    .col0(videocarta_1_out_40), .col1(videocarta_1_out_41), .col2(videocarta_1_out_42),
    .col3(videocarta_1_out_44), .col4(videocarta_1_out_46), .col5(videocarta_1_out_48),
    .col6(videocarta_1_out_50), .col7(videocarta_1_out_52), .col8(videocarta_1_out_54),
    .col9(videocarta_1_out_56), .col10(videocarta_1_out_58), .col11(videocarta_1_out_60),
    .col12(videocarta_1_out_62), .col13(videocarta_1_out_64), .col14(videocarta_1_out_66),
    .col15(videocarta_1_out_68), .col16(videocarta_1_out_43), .col17(videocarta_1_out_45),
    .col18(videocarta_1_out_47), .col19(videocarta_1_out_49), .col20(videocarta_1_out_51),
    .col21(videocarta_1_out_53), .col22(videocarta_1_out_55), .col23(videocarta_1_out_57),
    .col24(videocarta_1_out_59), .col25(videocarta_1_out_61), .col26(videocarta_1_out_63),
    .col27(videocarta_1_out_65), .col28(videocarta_1_out_67), .col29(videocarta_1_out_69),
    .col30(videocarta_1_out_70), .col31(videocarta_1_out_71));
  DotMatrix #(.matrixcols(4), .matrixrows(4)) dotmatrix_31 (
    .col0(borders_1_bus_0_146), .col1(borders_1_bus_0_147), .col2(borders_1_bus_0_148),
    .col3(borders_1_bus_0_153));
  DotMatrix #(.matrixcols(4), .matrixrows(4)) dotmatrix_32 (
    .col0(borders_1_bus_0_150), .col1(borders_1_bus_0_151), .col2(borders_1_bus_0_152),
    .col3(borders_1_bus_0_168));
  menu menu_1 (
    .\клавиатура (keyboard_1_data), .\меню_игра (\меню_игра ), ._1_2_p(_1_2p), .\_1_2_p_выбор (\_1_2_выбор ));  // open: пауза_игра
  DotMatrix #(.matrixcols(4), .matrixrows(4)) dotmatrix_33 (
    .col0(borders_1_bus_0_13), .col1(borders_1_bus_0_31), .col2(borders_1_bus_0_49), .col3(borders_1_bus_0_67));
  DotMatrix #(.matrixcols(4), .matrixrows(4)) dotmatrix_34 (
    .col0(borders_1_bus_0_12), .col1(borders_1_bus_0_30), .col2(borders_1_bus_0_48), .col3(borders_1_bus_0_66));
  DotMatrix #(.matrixcols(4), .matrixrows(4)) dotmatrix_35 (
    .col0(borders_1_bus_0_149), .col1(borders_1_bus_0_169), .col2(borders_1_bus_0_170),
    .col3(borders_1_bus_0_171));
  DotMatrix #(.matrixcols(4), .matrixrows(4)) dotmatrix_36 (
    .col0(borders_1_bus_0_164), .col1(borders_1_bus_0_165), .col2(borders_1_bus_0_166),
    .col3(borders_1_bus_0_167));
  bigc bigc_1 (
    .\клавиатура (keyboard_1_data), .\рядом_слева (\рядом_слева ), .x1(x1), .x2(x2), .y(y), .out_L(lbat),
    .\рядом_справа (\рядом_справа ), .out_R(rbat), .restart(score_1_restart));
  DotMatrix #(.matrixcols(4), .matrixrows(4)) dotmatrix_37 (
    .col0(borders_1_bus_0_15), .col1(borders_1_bus_0_33), .col2(borders_1_bus_0_51), .col3(borders_1_bus_0_69));
  DotMatrix #(.matrixcols(4), .matrixrows(4)) dotmatrix_38 (
    .col0(borders_1_bus_0_14), .col1(borders_1_bus_0_32), .col2(borders_1_bus_0_50), .col3(borders_1_bus_0_68));
  DotMatrix #(.matrixcols(4), .matrixrows(4)) dotmatrix_39 (
    .col0(borders_1_bus_0_182), .col1(borders_1_bus_0_183), .col2(borders_1_bus_0_184),
    .col3(borders_1_bus_0_185));
  DotMatrix #(.matrixcols(4), .matrixrows(4)) dotmatrix_40 (
    .col0(borders_1_bus_0_186), .col1(borders_1_bus_0_187), .col2(borders_1_bus_0_188),
    .col3(borders_1_bus_0_189));
  DotMatrix #(.matrixcols(4), .matrixrows(4)) dotmatrix_41 (
    .col0(borders_1_bus_0_16), .col1(borders_1_bus_0_34), .col2(borders_1_bus_0_52), .col3(borders_1_bus_0_70));
  DotMatrix #(.matrixcols(4), .matrixrows(4)) dotmatrix_42 (
    .col0(borders_1_bus_0_17), .col1(borders_1_bus_0_35), .col2(borders_1_bus_0_53), .col3(borders_1_bus_0_71));
  DotMatrix #(.matrixcols(4), .matrixrows(4)) dotmatrix_43 (
    .col0(borders_1_bus_0_204), .col1(borders_1_bus_0_205), .col2(borders_1_bus_0_206),
    .col3(borders_1_bus_0_207));
  DotMatrix #(.matrixcols(4), .matrixrows(4)) dotmatrix_44 (
    .col0(borders_1_bus_0_200), .col1(borders_1_bus_0_201), .col2(borders_1_bus_0_202),
    .col3(borders_1_bus_0_203));
  score score_1 (
    .restart(score_1_restart), .\рядом_справа (\рядом_справа ), .x(x1), .\рядом_слева (\рядом_слева ),
    .\счет_слева_единицы (\слева_единицы ), .x2(x2), .\счет_слева_десятки (\слева_десятки ),
    .\счет_справа_единицы (\справа_единицы ), .\счет_справа_десятки (\справа_десятки ));
  DotMatrix #(.matrixcols(4), .matrixrows(4)) dotmatrix_45 (
    .col0(borders_1_bus_0_18), .col1(borders_1_bus_0_36), .col2(borders_1_bus_0_54), .col3(borders_1_bus_0_72));
  DotMatrix #(.matrixcols(4), .matrixrows(4)) dotmatrix_46 (
    .col0(borders_1_bus_0_74), .col1(borders_1_bus_0_76), .col2(borders_1_bus_0_78), .col3(borders_1_bus_0_80));
  DotMatrix #(.matrixcols(4), .matrixrows(4)) dotmatrix_47 (
    .col0(borders_1_bus_0_82), .col1(borders_1_bus_0_84), .col2(borders_1_bus_0_86), .col3(borders_1_bus_0_88));
  DotMatrix #(.matrixcols(4), .matrixrows(4)) dotmatrix_48 (
    .col0(borders_1_bus_0_90), .col1(borders_1_bus_0_92), .col2(borders_1_bus_0_94), .col3(borders_1_bus_0_96));
  DotMatrix #(.matrixcols(4), .matrixrows(4)) dotmatrix_49 (
    .col0(borders_1_bus_0_98), .col1(borders_1_bus_0_100), .col2(borders_1_bus_0_102),
    .col3(borders_1_bus_0_104));
  DotMatrix #(.matrixcols(4), .matrixrows(4)) dotmatrix_50 (
    .col0(borders_1_bus_0_106), .col1(borders_1_bus_0_108), .col2(borders_1_bus_0_110),
    .col3(borders_1_bus_0_112));
  DotMatrix #(.matrixcols(4), .matrixrows(4)) dotmatrix_51 (
    .col0(borders_1_bus_0_114), .col1(borders_1_bus_0_116), .col2(borders_1_bus_0_118),
    .col3(borders_1_bus_0_120));
  DotMatrix #(.matrixcols(4), .matrixrows(4)) dotmatrix_52 (
    .col0(borders_1_bus_0_122), .col1(borders_1_bus_0_124), .col2(borders_1_bus_0_126),
    .col3(borders_1_bus_0_128));
  DotMatrix #(.matrixcols(4), .matrixrows(4)) dotmatrix_53 (
    .col0(borders_1_bus_0_130), .col1(borders_1_bus_0_132), .col2(borders_1_bus_0_134),
    .col3(borders_1_bus_0_136));
  DotMatrix #(.matrixcols(4), .matrixrows(4)) dotmatrix_54 (
    .col0(borders_1_bus_0_154), .col1(borders_1_bus_0_172), .col2(borders_1_bus_0_190),
    .col3(borders_1_bus_0_208));
  Hex_Digit_Display hex_digit_display_3 (.value(\справа_единицы ));  // open: dp
  Hex_Digit_Display hex_digit_display_4 (.value(\справа_десятки ));  // open: dp
endmodule

module videocarta (
  input  [31:0] palka_left,
  input  \меню_игра ,
  input  _1_2_p,
  input  [31:0] y,
  input  [31:0] x,
  input  [31:0] x2,
  input  [31:0] palka_right,
  output [31:0] out_8,
  output [31:0] out_9,
  output [31:0] out_10,
  output [31:0] out_11,
  output [31:0] out_12,
  output [31:0] out_13,
  output [31:0] out_14,
  output [31:0] out_15,
  output [31:0] out_16,
  output [31:0] out_17,
  output [31:0] out_18,
  output [31:0] out_19,
  output [31:0] out_20,
  output [31:0] out_21,
  output [31:0] out_22,
  output [31:0] out_23,
  output [31:0] out_24,
  output [31:0] out_25,
  output [31:0] out_26,
  output [31:0] out_27,
  output [31:0] out_28,
  output [31:0] out_29,
  output [31:0] out_30,
  output [31:0] out_31,
  output [31:0] out_32,
  output [31:0] out_33,
  output [31:0] out_34,
  output [31:0] out_35,
  output [31:0] out_36,
  output [31:0] out_37,
  output [31:0] out_38,
  output [31:0] out_39,
  output [31:0] out_40,
  output [31:0] out_41,
  output [31:0] out_42,
  output [31:0] out_43,
  output [31:0] out_44,
  output [31:0] out_45,
  output [31:0] out_46,
  output [31:0] out_47,
  output [31:0] out_48,
  output [31:0] out_49,
  output [31:0] out_50,
  output [31:0] out_51,
  output [31:0] out_52,
  output [31:0] out_53,
  output [31:0] out_54,
  output [31:0] out_55,
  output [31:0] out_56,
  output [31:0] out_57,
  output [31:0] out_58,
  output [31:0] out_59,
  output [31:0] out_60,
  output [31:0] out_61,
  output [31:0] out_62,
  output [31:0] out_63,
  output [31:0] out_64,
  output [31:0] out_65,
  output [31:0] out_66,
  output [31:0] out_67,
  output [31:0] out_68,
  output [31:0] out_69,
  output [31:0] out_70,
  output [31:0] out_71
);

  wire [0:0] multiplexer_1_out, multiplexer_2_out, multiplexer_3_out, multiplexer_4_out, multiplexer_5_out,
       multiplexer_6_out, multiplexer_7_out, multiplexer_8_out, multiplexer_9_out, multiplexer_10_out,
       multiplexer_11_out, multiplexer_12_out, multiplexer_13_out, multiplexer_14_out, multiplexer_15_out,
       multiplexer_16_out, multiplexer_17_out, multiplexer_18_out, multiplexer_19_out, multiplexer_20_out,
       multiplexer_21_out, multiplexer_22_out, multiplexer_23_out, multiplexer_24_out, multiplexer_25_out,
       multiplexer_26_out, multiplexer_27_out, multiplexer_28_out, multiplexer_29_out, multiplexer_30_out,
       multiplexer_31_out, multiplexer_65_out, multiplexer_66_out, multiplexer_67_out, multiplexer_68_out,
       multiplexer_69_out, multiplexer_70_out, multiplexer_71_out, multiplexer_72_out, multiplexer_73_out,
       multiplexer_74_out, multiplexer_75_out, multiplexer_76_out, multiplexer_77_out, multiplexer_78_out,
       multiplexer_79_out, multiplexer_80_out, multiplexer_81_out, multiplexer_82_out, multiplexer_83_out,
       multiplexer_84_out, multiplexer_85_out, multiplexer_86_out, multiplexer_87_out, multiplexer_88_out,
       multiplexer_89_out, multiplexer_90_out, multiplexer_91_out, multiplexer_92_out, multiplexer_93_out,
       multiplexer_94_out, multiplexer_95_out;
  wire [31:0] multiplexer_64_out, multiplexer_112_out, or_1_out, or_2_out, or_3_out, or_4_out;

  Multiplexer #(.enable("false")) multiplexer_1 (
    .in0(_1_2_p), .in1(x[1]), .out(multiplexer_1_out[0]), .sel(\меню_игра ));
  Multiplexer #(.enable("false")) multiplexer_2 (
    .in0(_1_2_p), .in1(x[2]), .out(multiplexer_2_out[0]), .sel(\меню_игра ));
  Multiplexer #(.enable("false")) multiplexer_3 (
    .in0(_1_2_p), .in1(x[3]), .out(multiplexer_3_out[0]), .sel(\меню_игра ));
  Multiplexer #(.enable("false")) multiplexer_4 (
    .in0(_1_2_p), .in1(x[4]), .out(multiplexer_4_out[0]), .sel(\меню_игра ));
  Multiplexer #(.enable("false")) multiplexer_5 (
    .in0(_1_2_p), .in1(x[5]), .out(multiplexer_5_out[0]), .sel(\меню_игра ));
  Multiplexer #(.enable("false")) multiplexer_6 (
    .in0(_1_2_p), .in1(x[6]), .out(multiplexer_6_out[0]), .sel(\меню_игра ));
  Multiplexer #(.enable("false")) multiplexer_7 (
    .in0(_1_2_p), .in1(x[7]), .out(multiplexer_7_out[0]), .sel(\меню_игра ));
  Multiplexer #(.enable("false")) multiplexer_8 (
    .in0(_1_2_p), .in1(x[8]), .out(multiplexer_8_out[0]), .sel(\меню_игра ));
  Multiplexer #(.enable("false")) multiplexer_9 (
    .in0(_1_2_p), .in1(x[9]), .out(multiplexer_9_out[0]), .sel(\меню_игра ));
  Multiplexer #(.enable("false")) multiplexer_10 (
    .in0(_1_2_p), .in1(x[10]), .out(multiplexer_10_out[0]), .sel(\меню_игра ));
  Multiplexer #(.enable("false")) multiplexer_11 (
    .in0(_1_2_p), .in1(x[11]), .out(multiplexer_11_out[0]), .sel(\меню_игра ));
  Multiplexer #(.enable("false")) multiplexer_12 (
    .in0(_1_2_p), .in1(x[12]), .out(multiplexer_12_out[0]), .sel(\меню_игра ));
  Multiplexer #(.enable("false")) multiplexer_13 (
    .in0(_1_2_p), .in1(x[13]), .out(multiplexer_13_out[0]), .sel(\меню_игра ));
  Multiplexer #(.enable("false")) multiplexer_14 (
    .in0(_1_2_p), .in1(x[14]), .out(multiplexer_14_out[0]), .sel(\меню_игра ));
  Multiplexer #(.enable("false")) multiplexer_15 (
    .in0(_1_2_p), .in1(x[15]), .out(multiplexer_15_out[0]), .sel(\меню_игра ));
  Multiplexer #(.enable("false")) multiplexer_16 (
    .in0(_1_2_p), .in1(x2[0]), .out(multiplexer_16_out[0]), .sel(\меню_игра ));
  Multiplexer #(.enable("false")) multiplexer_17 (
    .in0(_1_2_p), .in1(x2[1]), .out(multiplexer_17_out[0]), .sel(\меню_игра ));
  Multiplexer #(.enable("false")) multiplexer_18 (
    .in0(_1_2_p), .in1(x2[2]), .out(multiplexer_18_out[0]), .sel(\меню_игра ));
  Multiplexer #(.enable("false")) multiplexer_19 (
    .in0(_1_2_p), .in1(x2[3]), .out(multiplexer_19_out[0]), .sel(\меню_игра ));
  Multiplexer #(.enable("false")) multiplexer_20 (
    .in0(_1_2_p), .in1(x2[4]), .out(multiplexer_20_out[0]), .sel(\меню_игра ));
  Multiplexer #(.enable("false")) multiplexer_21 (
    .in0(_1_2_p), .in1(x2[5]), .out(multiplexer_21_out[0]), .sel(\меню_игра ));
  Multiplexer #(.enable("false")) multiplexer_22 (
    .in0(_1_2_p), .in1(x2[6]), .out(multiplexer_22_out[0]), .sel(\меню_игра ));
  Multiplexer #(.enable("false")) multiplexer_23 (
    .in0(_1_2_p), .in1(x2[7]), .out(multiplexer_23_out[0]), .sel(\меню_игра ));
  Multiplexer #(.enable("false")) multiplexer_24 (
    .in0(_1_2_p), .in1(x2[8]), .out(multiplexer_24_out[0]), .sel(\меню_игра ));
  Multiplexer #(.enable("false")) multiplexer_25 (
    .in0(_1_2_p), .in1(x2[9]), .out(multiplexer_25_out[0]), .sel(\меню_игра ));
  Multiplexer #(.enable("false")) multiplexer_26 (
    .in0(_1_2_p), .in1(x2[10]), .out(multiplexer_26_out[0]), .sel(\меню_игра ));
  Multiplexer #(.enable("false")) multiplexer_27 (
    .in0(_1_2_p), .in1(x2[11]), .out(multiplexer_27_out[0]), .sel(\меню_игра ));
  Multiplexer #(.enable("false")) multiplexer_28 (
    .in0(_1_2_p), .in1(x2[12]), .out(multiplexer_28_out[0]), .sel(\меню_игра ));
  Multiplexer #(.enable("false")) multiplexer_29 (
    .in0(_1_2_p), .in1(x2[13]), .out(multiplexer_29_out[0]), .sel(\меню_игра ));
  Multiplexer #(.enable("false")) multiplexer_30 (
    .in0(_1_2_p), .in1(x2[14]), .out(multiplexer_30_out[0]), .sel(\меню_игра ));
  Multiplexer #(.enable("false")) multiplexer_31 (
    .in0(_1_2_p), .in1(x2[15]), .out(multiplexer_31_out[0]), .sel(\меню_игра ));
  assign or_1_out = palka_left | {32{1'b0}};  // OR_Gate or_1, 32 bits wide
  assign or_2_out = y | palka_left;  // OR_Gate or_2, 32 bits wide
  Multiplexer #(.select(2), .width(32), .enable("false")) multiplexer_32 (
    .in0(32'hfe07c110), .in1(32'hfe0441f0), .in2({32{1'b0}}), .in3(y), .out(out_9),
    .sel({\меню_игра , multiplexer_1_out[0]}));
  Multiplexer #(.select(2), .width(32), .enable("false")) multiplexer_33 (
    .in0(32'h9007c110), .in1(32'h900441f0), .in2({32{1'b0}}), .in3(y), .out(out_10),
    .sel({\меню_игра , multiplexer_2_out[0]}));
  Multiplexer #(.select(2), .width(32), .enable("false")) multiplexer_34 (
    .in0(32'h9007c110), .in1(32'h900441f0), .in2({32{1'b0}}), .in3(y), .out(out_12),
    .sel({\меню_игра , multiplexer_3_out[0]}));
  Multiplexer #(.select(2), .width(32), .enable("false")) multiplexer_35 (
    .in0(32'h600380e0), .in1(32'h600380e0), .in2({32{1'b0}}), .in3(y), .out(out_14),
    .sel({\меню_игра , multiplexer_4_out[0]}));
  Multiplexer #(.select(2), .width(32), .enable("false")) multiplexer_36 (
    .in0({32{1'b0}}), .in1({32{1'b0}}), .in2({32{1'b0}}), .in3(y), .out(out_16),
    .sel({\меню_игра , multiplexer_5_out[0]}));
  Multiplexer #(.select(2), .width(32), .enable("false")) multiplexer_37 (
    .in0(32'h2e000118), .in1(32'h2e000118), .in2({32{1'b0}}), .in3(y), .out(out_18),
    .sel({\меню_игра , multiplexer_6_out[0]}));
  Multiplexer #(.select(2), .width(32), .enable("false")) multiplexer_38 (
    .in0(32'h22228), .in1(32'h22228), .in2({32{1'b0}}), .in3(y), .out(out_20),
    .sel({\меню_игра , multiplexer_7_out[0]}));
  Multiplexer #(.select(2), .width(32), .enable("false")) multiplexer_39 (
    .in0(32'h3e042248), .in1(32'h3e042248), .in2({32{1'b0}}), .in3(y), .out(out_22),
    .sel({\меню_игра , multiplexer_8_out[0]}));
  Multiplexer #(.select(2), .width(32), .enable("false")) multiplexer_40 (
    .in0(32'h100fe248), .in1(32'h100fe248), .in2({32{1'b0}}), .in3(y), .out(out_24),
    .sel({\меню_игра , multiplexer_9_out[0]}));
  Multiplexer #(.select(2), .width(32), .enable("false")) multiplexer_41 (
    .in0(32'h20002188), .in1(32'h20002188), .in2({32{1'b0}}), .in3(y), .out(out_26),
    .sel({\меню_игра , multiplexer_10_out[0]}));
  Multiplexer #(.select(2), .width(32), .enable("false")) multiplexer_42 (
    .in0(32'h1e002000), .in1(32'h1e002000), .in2({32{1'b0}}), .in3(y), .out(out_28),
    .sel({\меню_игра , multiplexer_11_out[0]}));
  Multiplexer #(.select(2), .width(32), .enable("false")) multiplexer_43 (
    .in0(32'h3f8), .in1(32'h3f8), .in2({32{1'b0}}), .in3(y), .out(out_30),
    .sel({\меню_игра , multiplexer_12_out[0]}));
  Multiplexer #(.select(2), .width(32), .enable("false")) multiplexer_44 (
    .in0(32'h1e800240), .in1(32'h1e800240), .in2({32{1'b0}}), .in3(y), .out(out_32),
    .sel({\меню_игра , multiplexer_13_out[0]}));
  Multiplexer #(.select(2), .width(32), .enable("false")) multiplexer_45 (
    .in0(32'h124fe240), .in1(32'h124fe240), .in2({32{1'b0}}), .in3(y), .out(out_34),
    .sel({\меню_игра , multiplexer_14_out[0]}));
  Multiplexer #(.select(2), .width(32), .enable("false")) multiplexer_46 (
    .in0(32'h12490180), .in1(32'h12490180), .in2({32{1'b0}}), .in3(y), .out(out_36),
    .sel({\меню_игра , multiplexer_15_out[0]}));
  Multiplexer #(.select(2), .width(32), .enable("false")) multiplexer_47 (
    .in0(32'h1002a040), .in1(32'h1002a040), .in2({32{1'b0}}), .in3(y), .out(out_40),
    .sel({\меню_игра , multiplexer_16_out[0]}));
  Multiplexer #(.select(2), .width(32), .enable("false")) multiplexer_48 (
    .in0(32'h2002a000), .in1(32'h2002a000), .in2({32{1'b0}}), .in3(y), .out(out_41),
    .sel({\меню_игра , multiplexer_17_out[0]}));
  Multiplexer #(.select(2), .width(32), .enable("false")) multiplexer_49 (
    .in0(32'h1e0100f8), .in1(32'h1e0100f8), .in2({32{1'b0}}), .in3(y), .out(out_42),
    .sel({\меню_игра , multiplexer_18_out[0]}));
  Multiplexer #(.select(2), .width(32), .enable("false")) multiplexer_50 (
    .in0(32'h40), .in1(32'h40), .in2({32{1'b0}}), .in3(y), .out(out_44),
    .sel({\меню_игра , multiplexer_19_out[0]}));
  Multiplexer #(.select(2), .width(32), .enable("false")) multiplexer_51 (
    .in0(32'hc83e080), .in1(32'hc83e080), .in2({32{1'b0}}), .in3(y), .out(out_46),
    .sel({\меню_игра , multiplexer_20_out[0]}));
  Multiplexer #(.select(2), .width(32), .enable("false")) multiplexer_52 (
    .in0(32'h12410080), .in1(32'h12410080), .in2({32{1'b0}}), .in3(y), .out(out_48),
    .sel({\меню_игра , multiplexer_21_out[0]}));
  Multiplexer #(.select(2), .width(32), .enable("false")) multiplexer_53 (
    .in0(32'h12420000), .in1(32'h12420000), .in2({32{1'b0}}), .in3(y), .out(out_50),
    .sel({\меню_игра , multiplexer_22_out[0]}));
  Multiplexer #(.select(2), .width(32), .enable("false")) multiplexer_54 (
    .in0(32'h3fc20048), .in1(32'h3fc20048), .in2({32{1'b0}}), .in3(y), .out(out_52),
    .sel({\меню_игра , multiplexer_23_out[0]}));
  Multiplexer #(.select(2), .width(32), .enable("false")) multiplexer_55 (
    .in0(32'ha8), .in1(32'ha8), .in2({32{1'b0}}), .in3(y), .out(out_54),
    .sel({\меню_игра , multiplexer_24_out[0]}));
  Multiplexer #(.select(2), .width(32), .enable("false")) multiplexer_56 (
    .in0(32'ha8), .in1(32'ha8), .in2({32{1'b0}}), .in3(y), .out(out_56),
    .sel({\меню_игра , multiplexer_25_out[0]}));
  Multiplexer #(.select(2), .width(32), .enable("false")) multiplexer_57 (
    .in0(32'h90), .in1(32'h90), .in2({32{1'b0}}), .in3(y), .out(out_58),
    .sel({\меню_игра , multiplexer_26_out[0]}));
  Multiplexer #(.select(2), .width(32), .enable("false")) multiplexer_58 (
    .in0({32{1'b0}}), .in1({32{1'b0}}), .in2({32{1'b0}}), .in3(y), .out(out_60),
    .sel({\меню_игра , multiplexer_27_out[0]}));
  Multiplexer #(.select(2), .width(32), .enable("false")) multiplexer_59 (
    .in0({32{1'b1}}), .in1({32{1'b1}}), .in2({32{1'b0}}), .in3(y), .out(out_62),
    .sel({\меню_игра , multiplexer_28_out[0]}));
  Multiplexer #(.select(2), .width(32), .enable("false")) multiplexer_60 (
    .in0({32{1'b0}}), .in1({32{1'b0}}), .in2({32{1'b0}}), .in3(y), .out(out_64),
    .sel({\меню_игра , multiplexer_29_out[0]}));
  Multiplexer #(.select(2), .width(32), .enable("false")) multiplexer_61 (
    .in0(32'h1fc7c03), .in1(32'h1fc7c03), .in2({32{1'b0}}), .in3(y), .out(out_66),
    .sel({\меню_игра , multiplexer_30_out[0]}));
  Multiplexer #(.select(2), .width(32), .enable("false")) multiplexer_62 (
    .in0(32'h1248241), .in1(32'h1248241), .in2({32{1'b0}}), .in3(y), .out(out_68),
    .sel({\меню_игра , multiplexer_31_out[0]}));
  Multiplexer #(.select(2), .width(32), .enable("false")) multiplexer_63 (
    .in0(32'h380e0), .in1(32'h380e0), .in2(multiplexer_64_out), .in3(multiplexer_64_out), .out(out_8),
    .sel({\меню_игра , _1_2_p}));
  Multiplexer #(.width(32), .enable("false")) multiplexer_64 (
    .in0(or_1_out), .in1(or_2_out), .out(multiplexer_64_out), .sel(x[0]));
  Multiplexer #(.enable("false")) multiplexer_65 (
    .in0(_1_2_p), .in1(x[16]), .out(multiplexer_65_out[0]), .sel(\меню_игра ));
  Multiplexer #(.enable("false")) multiplexer_66 (
    .in0(_1_2_p), .in1(x[17]), .out(multiplexer_66_out[0]), .sel(\меню_игра ));
  Multiplexer #(.enable("false")) multiplexer_67 (
    .in0(_1_2_p), .in1(x[18]), .out(multiplexer_67_out[0]), .sel(\меню_игра ));
  Multiplexer #(.enable("false")) multiplexer_68 (
    .in0(_1_2_p), .in1(x[19]), .out(multiplexer_68_out[0]), .sel(\меню_игра ));
  Multiplexer #(.enable("false")) multiplexer_69 (
    .in0(_1_2_p), .in1(x[20]), .out(multiplexer_69_out[0]), .sel(\меню_игра ));
  Multiplexer #(.enable("false")) multiplexer_70 (
    .in0(_1_2_p), .in1(x[21]), .out(multiplexer_70_out[0]), .sel(\меню_игра ));
  Multiplexer #(.enable("false")) multiplexer_71 (
    .in0(_1_2_p), .in1(x[22]), .out(multiplexer_71_out[0]), .sel(\меню_игра ));
  Multiplexer #(.enable("false")) multiplexer_72 (
    .in0(_1_2_p), .in1(x[23]), .out(multiplexer_72_out[0]), .sel(\меню_игра ));
  Multiplexer #(.enable("false")) multiplexer_73 (
    .in0(_1_2_p), .in1(x[24]), .out(multiplexer_73_out[0]), .sel(\меню_игра ));
  Multiplexer #(.enable("false")) multiplexer_74 (
    .in0(_1_2_p), .in1(x[25]), .out(multiplexer_74_out[0]), .sel(\меню_игра ));
  Multiplexer #(.enable("false")) multiplexer_75 (
    .in0(_1_2_p), .in1(x[26]), .out(multiplexer_75_out[0]), .sel(\меню_игра ));
  Multiplexer #(.enable("false")) multiplexer_76 (
    .in0(_1_2_p), .in1(x[27]), .out(multiplexer_76_out[0]), .sel(\меню_игра ));
  Multiplexer #(.enable("false")) multiplexer_77 (
    .in0(_1_2_p), .in1(x[28]), .out(multiplexer_77_out[0]), .sel(\меню_игра ));
  Multiplexer #(.enable("false")) multiplexer_78 (
    .in0(_1_2_p), .in1(x[29]), .out(multiplexer_78_out[0]), .sel(\меню_игра ));
  Multiplexer #(.enable("false")) multiplexer_79 (
    .in0(_1_2_p), .in1(x[30]), .out(multiplexer_79_out[0]), .sel(\меню_игра ));
  Multiplexer #(.enable("false")) multiplexer_80 (
    .in0(_1_2_p), .in1(x[31]), .out(multiplexer_80_out[0]), .sel(\меню_игра ));
  Multiplexer #(.enable("false")) multiplexer_81 (
    .in0(_1_2_p), .in1(x2[16]), .out(multiplexer_81_out[0]), .sel(\меню_игра ));
  Multiplexer #(.enable("false")) multiplexer_82 (
    .in0(_1_2_p), .in1(x2[17]), .out(multiplexer_82_out[0]), .sel(\меню_игра ));
  Multiplexer #(.enable("false")) multiplexer_83 (
    .in0(_1_2_p), .in1(x2[18]), .out(multiplexer_83_out[0]), .sel(\меню_игра ));
  Multiplexer #(.enable("false")) multiplexer_84 (
    .in0(_1_2_p), .in1(x2[19]), .out(multiplexer_84_out[0]), .sel(\меню_игра ));
  Multiplexer #(.enable("false")) multiplexer_85 (
    .in0(_1_2_p), .in1(x2[20]), .out(multiplexer_85_out[0]), .sel(\меню_игра ));
  Multiplexer #(.enable("false")) multiplexer_86 (
    .in0(_1_2_p), .in1(x2[21]), .out(multiplexer_86_out[0]), .sel(\меню_игра ));
  Multiplexer #(.enable("false")) multiplexer_87 (
    .in0(_1_2_p), .in1(x2[22]), .out(multiplexer_87_out[0]), .sel(\меню_игра ));
  Multiplexer #(.enable("false")) multiplexer_88 (
    .in0(_1_2_p), .in1(x2[23]), .out(multiplexer_88_out[0]), .sel(\меню_игра ));
  Multiplexer #(.enable("false")) multiplexer_89 (
    .in0(_1_2_p), .in1(x2[24]), .out(multiplexer_89_out[0]), .sel(\меню_игра ));
  Multiplexer #(.enable("false")) multiplexer_90 (
    .in0(_1_2_p), .in1(x2[25]), .out(multiplexer_90_out[0]), .sel(\меню_игра ));
  Multiplexer #(.enable("false")) multiplexer_91 (
    .in0(_1_2_p), .in1(x2[26]), .out(multiplexer_91_out[0]), .sel(\меню_игра ));
  Multiplexer #(.enable("false")) multiplexer_92 (
    .in0(_1_2_p), .in1(x2[27]), .out(multiplexer_92_out[0]), .sel(\меню_игра ));
  Multiplexer #(.enable("false")) multiplexer_93 (
    .in0(_1_2_p), .in1(x2[28]), .out(multiplexer_93_out[0]), .sel(\меню_игра ));
  Multiplexer #(.enable("false")) multiplexer_94 (
    .in0(_1_2_p), .in1(x2[29]), .out(multiplexer_94_out[0]), .sel(\меню_игра ));
  Multiplexer #(.enable("false")) multiplexer_95 (
    .in0(_1_2_p), .in1(x2[30]), .out(multiplexer_95_out[0]), .sel(\меню_игра ));
  assign or_3_out = palka_right | {32{1'b0}};  // OR_Gate or_3, 32 bits wide
  assign or_4_out = y | palka_right;  // OR_Gate or_4, 32 bits wide
  Multiplexer #(.select(2), .width(32), .enable("false")) multiplexer_96 (
    .in0(32'h124927f), .in1(32'h124927f), .in2({32{1'b0}}), .in3(y), .out(out_43),
    .sel({\меню_игра , multiplexer_81_out[0]}));
  Multiplexer #(.select(2), .width(32), .enable("false")) multiplexer_97 (
    .in0(32'h9c40), .in1(32'h9c40), .in2({32{1'b0}}), .in3(y), .out(out_45),
    .sel({\меню_игра , multiplexer_82_out[0]}));
  Multiplexer #(.select(2), .width(32), .enable("false")) multiplexer_98 (
    .in0(32'h320000), .in1(32'h320000), .in2({32{1'b0}}), .in3(y), .out(out_47),
    .sel({\меню_игра , multiplexer_83_out[0]}));
  Multiplexer #(.select(2), .width(32), .enable("false")) multiplexer_99 (
    .in0(32'h4a3e1f), .in1(32'h4a3e1f), .in2({32{1'b0}}), .in3(y), .out(out_49),
    .sel({\меню_игра , multiplexer_84_out[0]}));
  Multiplexer #(.select(2), .width(32), .enable("false")) multiplexer_100 (
    .in0(32'hf84a0001), .in1(32'hf84a0001), .in2({32{1'b0}}), .in3(y), .out(out_51),
    .sel({\меню_игра , multiplexer_85_out[0]}));
  Multiplexer #(.select(2), .width(32), .enable("false")) multiplexer_101 (
    .in0(32'ha87c1c01), .in1(32'ha87c1c01), .in2({32{1'b0}}), .in3(y), .out(out_53),
    .sel({\меню_игра , multiplexer_86_out[0]}));
  Multiplexer #(.select(2), .width(32), .enable("false")) multiplexer_102 (
    .in0(32'h50002a1f), .in1(32'h50002a1f), .in2({32{1'b0}}), .in3(y), .out(out_55),
    .sel({\меню_игра , multiplexer_87_out[0]}));
  Multiplexer #(.select(2), .width(32), .enable("false")) multiplexer_103 (
    .in0(32'h382a00), .in1(32'h382a00), .in2({32{1'b0}}), .in3(y), .out(out_57),
    .sel({\меню_игра , multiplexer_88_out[0]}));
  Multiplexer #(.select(2), .width(32), .enable("false")) multiplexer_104 (
    .in0(32'h8044101f), .in1(32'h8044101f), .in2({32{1'b0}}), .in3(y), .out(out_59),
    .sel({\меню_игра , multiplexer_89_out[0]}));
  Multiplexer #(.select(2), .width(32), .enable("false")) multiplexer_105 (
    .in0(32'h40440000), .in1(32'h40440000), .in2({32{1'b0}}), .in3(y), .out(out_61),
    .sel({\меню_игра , multiplexer_90_out[0]}));
  Multiplexer #(.select(2), .width(32), .enable("false")) multiplexer_106 (
    .in0(32'h38383e17), .in1(32'h38383e17), .in2({32{1'b0}}), .in3(y), .out(out_63),
    .sel({\меню_игра , multiplexer_91_out[0]}));
  Multiplexer #(.select(2), .width(32), .enable("false")) multiplexer_107 (
    .in0(32'h40000a00), .in1(32'h40000a00), .in2({32{1'b0}}), .in3(y), .out(out_65),
    .sel({\меню_игра , multiplexer_92_out[0]}));
  Multiplexer #(.select(2), .width(32), .enable("false")) multiplexer_108 (
    .in0(32'h807c0a12), .in1(32'h807c0a12), .in2({32{1'b0}}), .in3(y), .out(out_67),
    .sel({\меню_игра , multiplexer_93_out[0]}));
  Multiplexer #(.select(2), .width(32), .enable("false")) multiplexer_109 (
    .in0(32'h200415), .in1(32'h200415), .in2({32{1'b0}}), .in3(y), .out(out_69),
    .sel({\меню_игра , multiplexer_94_out[0]}));
  Multiplexer #(.select(2), .width(32), .enable("false")) multiplexer_110 (
    .in0(32'h400015), .in1(32'h400015), .in2({32{1'b0}}), .in3(y), .out(out_70),
    .sel({\меню_игра , multiplexer_95_out[0]}));
  Multiplexer #(.select(2), .width(32), .enable("false")) multiplexer_111 (
    .in0(32'h40000f), .in1(32'h40000f), .in2(multiplexer_112_out), .in3(multiplexer_112_out), .out(out_71),
    .sel({\меню_игра , _1_2_p}));
  Multiplexer #(.width(32), .enable("false")) multiplexer_112 (
    .in0(or_3_out), .in1(or_4_out), .out(multiplexer_112_out), .sel(x2[31]));
  Multiplexer #(.select(2), .width(32), .enable("false")) multiplexer_113 (
    .in0(32'h3fc90000), .in1(32'h3fc90000), .in2({32{1'b0}}), .in3(y), .out(out_11),
    .sel({\меню_игра , multiplexer_65_out[0]}));
  Multiplexer #(.select(2), .width(32), .enable("false")) multiplexer_114 (
    .in0(32'h600f8), .in1(32'h600f8), .in2({32{1'b0}}), .in3(y), .out(out_13),
    .sel({\меню_игра , multiplexer_66_out[0]}));
  Multiplexer #(.select(2), .width(32), .enable("false")) multiplexer_115 (
    .in0(32'h8000000), .in1(32'h8000000), .in2({32{1'b0}}), .in3(y), .out(out_15),
    .sel({\меню_игра , multiplexer_67_out[0]}));
  Multiplexer #(.select(2), .width(32), .enable("false")) multiplexer_116 (
    .in0(32'h803e090), .in1(32'h803e090), .in2({32{1'b0}}), .in3(y), .out(out_17),
    .sel({\меню_игра , multiplexer_68_out[0]}));
  Multiplexer #(.select(2), .width(32), .enable("false")) multiplexer_117 (
    .in0(32'ha8), .in1(32'ha8), .in2({32{1'b0}}), .in3(y), .out(out_19),
    .sel({\меню_игра , multiplexer_69_out[0]}));
  Multiplexer #(.select(2), .width(32), .enable("false")) multiplexer_118 (
    .in0(32'hfe0240a8), .in1(32'hfe0240a8), .in2({32{1'b0}}), .in3(y), .out(out_21),
    .sel({\меню_игра , multiplexer_70_out[0]}));
  Multiplexer #(.select(2), .width(32), .enable("false")) multiplexer_119 (
    .in0(32'h9002a078), .in1(32'h9002a078), .in2({32{1'b0}}), .in3(y), .out(out_23),
    .sel({\меню_игра , multiplexer_71_out[0]}));
  Multiplexer #(.select(2), .width(32), .enable("false")) multiplexer_120 (
    .in0(32'h9002a000), .in1(32'h9002a000), .in2({32{1'b0}}), .in3(y), .out(out_25),
    .sel({\меню_игра , multiplexer_72_out[0]}));
  Multiplexer #(.select(2), .width(32), .enable("false")) multiplexer_121 (
    .in0(32'h6001e0c8), .in1(32'h6001e0c8), .in2({32{1'b0}}), .in3(y), .out(out_27),
    .sel({\меню_игра , multiplexer_73_out[0]}));
  Multiplexer #(.select(2), .width(32), .enable("false")) multiplexer_122 (
    .in0(32'h28), .in1(32'h28), .in2({32{1'b0}}), .in3(y), .out(out_29),
    .sel({\меню_игра , multiplexer_74_out[0]}));
  Multiplexer #(.select(2), .width(32), .enable("false")) multiplexer_123 (
    .in0(32'h1c032028), .in1(32'h1c032028), .in2({32{1'b0}}), .in3(y), .out(out_31),
    .sel({\меню_игра , multiplexer_75_out[0]}));
  Multiplexer #(.select(2), .width(32), .enable("false")) multiplexer_124 (
    .in0(32'h2200a0f0), .in1(32'h2200a0f0), .in2({32{1'b0}}), .in3(y), .out(out_33),
    .sel({\меню_игра , multiplexer_76_out[0]}));
  Multiplexer #(.select(2), .width(32), .enable("false")) multiplexer_125 (
    .in0(32'h2200a000), .in1(32'h2200a000), .in2({32{1'b0}}), .in3(y), .out(out_35),
    .sel({\меню_игра , multiplexer_77_out[0]}));
  Multiplexer #(.select(2), .width(32), .enable("false")) multiplexer_126 (
    .in0(32'h1c03c070), .in1(32'h1c03c070), .in2({32{1'b0}}), .in3(y), .out(out_37),
    .sel({\меню_игра , multiplexer_78_out[0]}));
  Multiplexer #(.select(2), .width(32), .enable("false")) multiplexer_127 (
    .in0(32'ha8), .in1(32'ha8), .in2({32{1'b0}}), .in3(y), .out(out_38),
    .sel({\меню_игра , multiplexer_79_out[0]}));
  Multiplexer #(.select(2), .width(32), .enable("false")) multiplexer_128 (
    .in0(32'h3e01c0a8), .in1(32'h3e01c0a8), .in2({32{1'b0}}), .in3(y), .out(out_39),
    .sel({\меню_игра , multiplexer_80_out[0]}));
endmodule

module score (
  input  [31:0] x2,
  input  [31:0] x,
  output restart,
  output \рядом_справа ,
  output \рядом_слева ,
  output [3:0] \счет_справа_единицы ,
  output [3:0] \счет_справа_десятки ,
  output [3:0] \счет_слева_единицы ,
  output [3:0] \счет_слева_десятки 
);

  wire and_1_out, and_2_out, and_3_out, and_4_out, and_5_out, comparator_1_eq, comparator_2_eq,
       comparator_3_eq, comparator_4_eq, comparator_5_eq, comparator_6_eq, comparator_7_eq, comparator_8_eq,
       comparator_9_eq, comparator_10_eq, comparator_11_eq, comparator_12_eq, comparator_13_eq,
       comparator_14_eq, comparator_15_eq, comparator_16_eq, comparator_17_eq, comparator_18_eq, or_1_out,
       or_3_out, or_4_out, or_5_out, or_6_out, or_7_out, or_8_out, or_9_out, or_10_out, or_11_out;
  wire [3:0] adder_1_out, adder_2_out, adder_4_out, adder_5_out, adder_6_out, adder_8_out, register_1_q,
       register_3_q, subtractor_1_out, subtractor_2_out, \выл , \выпр , \сл1 , \спр1 ;

  Adder #(.width(4)) adder_1 (.a(register_1_q), .b(4'b0001), .out(adder_1_out));  // open: cin, cout
  Adder #(.width(4)) adder_2 (.a(register_1_q), .b(4'b0001), .out(adder_2_out));  // open: cin, cout
  Comparator #(.width(4)) comparator_1 (.a(4'b1010), .b(register_1_q), .eq(comparator_1_eq));  // open: gt, lt
  or or_1 (or_1_out, comparator_1_eq, or_4_out);
  or or_2 (restart, or_4_out, or_11_out);
  Register #(.width(4)) register_1 (.D(adder_2_out), .en(1'b1), .Q(register_1_q), .clk(and_3_out), .clr(or_1_out));
  Comparator #(.width(32)) comparator_2 (.a(32'h80000000), .b(x), .eq(comparator_2_eq));  // open: gt, lt
  Adder #(.width(4)) adder_3 (.a(\счет_справа_единицы ), .b(4'b0001), .out(\спр1 ));  // open: cin, cout
  Comparator #(.width(4)) comparator_3 (.a(4'b1010), .b(\счет_справа_единицы ), .eq(comparator_3_eq));  // open: gt, lt
  or or_3 (or_3_out, comparator_3_eq, or_4_out);
  Adder #(.width(4)) adder_4 (.a(register_3_q), .b(4'b0001), .out(adder_4_out));  // open: cin, cout
  Comparator #(.width(4)) comparator_4 (.a(4'b1010), .b(register_3_q), .eq(comparator_4_eq));  // open: gt, lt
  Adder #(.width(4)) adder_5 (.a(register_3_q), .b(4'b0001), .out(adder_5_out));  // open: cin, cout
  or or_4 (or_4_out, or_7_out, or_10_out);
  Register #(.width(4)) register_2 (
    .D(\выпр ), .en(1'b1), .Q(\счет_справа_единицы ), .clk(comparator_18_eq), .clr(or_3_out));
  Register #(.width(4)) register_3 (.D(adder_4_out), .en(1'b1), .Q(register_3_q), .clk(or_1_out), .clr(or_5_out));
  or or_5 (or_5_out, comparator_4_eq, or_4_out);
  Subtractor #(.width(4)) subtractor_1 (
    .a(\счет_справа_единицы ), .b(4'b0001), .out(subtractor_1_out));  // open: bin, bout
  Adder #(.width(4)) adder_6 (.a(\счет_справа_десятки ), .b(4'b0001), .out(adder_6_out));  // open: cin, cout
  Comparator #(.width(4)) comparator_5 (.a(4'b1010), .b(\счет_справа_десятки ), .eq(comparator_5_eq));  // open: gt, lt
  Comparator #(.width(4)) comparator_6 (.a(4'b1010), .b(\счет_справа_десятки ), .eq(comparator_6_eq));  // open: gt, lt
  Comparator #(.width(4)) comparator_7 (
    .a(\счет_справа_единицы ), .b(adder_1_out), .eq(comparator_7_eq));  // open: gt, lt
  Comparator #(.width(4)) comparator_8 (
    .a(\счет_справа_десятки ), .b(adder_5_out), .eq(comparator_8_eq));  // open: gt, lt
  Comparator #(.width(4)) comparator_9 (
    .a(\счет_справа_единицы ), .b(register_1_q), .eq(comparator_9_eq));  // open: gt, lt
  Comparator #(.width(32)) comparator_10 (.a(32'h1), .b(x2), .eq(comparator_10_eq));  // open: gt, lt
  Multiplexer #(.width(4)) multiplexer_1 (
    .in0(\спр1 ), .in1(subtractor_1_out), .out(\выпр ), .sel(comparator_2_eq));  // open: en
  Register #(.width(4)) register_4 (
    .D(adder_6_out), .en(1'b1), .Q(\счет_справа_десятки ), .clk(or_3_out), .clr(or_6_out));
  or or_6 (or_6_out, comparator_5_eq, or_4_out);
  and and_1 (and_1_out, comparator_7_eq, comparator_8_eq);
  and and_2 (and_2_out, comparator_8_eq, comparator_9_eq);
  or or_7 (or_7_out, comparator_6_eq, and_1_out);
  Adder #(.width(4)) adder_7 (.a(\счет_слева_единицы ), .b(4'b0001), .out(\сл1 ));  // open: cin, cout
  Comparator #(.width(4)) comparator_11 (.a(4'b1010), .b(\счет_слева_единицы ), .eq(comparator_11_eq));  // open: gt, lt
  and and_3 (and_3_out, and_2_out, and_5_out);
  Subtractor #(.width(4)) subtractor_2 (
    .a(\счет_слева_единицы ), .b(4'b0001), .out(subtractor_2_out));  // open: bin, bout
  Register #(.width(4)) register_5 (
    .D(\выл ), .en(1'b1), .Q(\счет_слева_единицы ), .clk(comparator_17_eq), .clr(or_8_out));
  or or_8 (or_8_out, comparator_11_eq, or_4_out);
  Multiplexer #(.width(4)) multiplexer_2 (
    .in0(\сл1 ), .in1(subtractor_2_out), .out(\выл ), .sel(comparator_10_eq));  // open: en
  Adder #(.width(4)) adder_8 (.a(\счет_слева_десятки ), .b(4'b0001), .out(adder_8_out));  // open: cin, cout
  Comparator #(.width(4)) comparator_12 (.a(4'b1010), .b(\счет_слева_десятки ), .eq(comparator_12_eq));  // open: gt, lt
  Comparator #(.width(4)) comparator_13 (
    .a(\счет_слева_единицы ), .b(adder_1_out), .eq(comparator_13_eq));  // open: gt, lt
  Comparator #(.width(4)) comparator_14 (
    .a(\счет_слева_десятки ), .b(adder_5_out), .eq(comparator_14_eq));  // open: gt, lt
  Comparator #(.width(4)) comparator_15 (
    .a(\счет_слева_единицы ), .b(register_1_q), .eq(comparator_15_eq));  // open: gt, lt
  Register #(.width(4)) register_6 (
    .D(adder_8_out), .en(1'b1), .Q(\счет_слева_десятки ), .clk(or_8_out), .clr(or_9_out));
  or or_9 (or_9_out, comparator_12_eq, or_4_out);
  Comparator #(.width(4)) comparator_16 (.a(4'b1010), .b(\счет_слева_десятки ), .eq(comparator_16_eq));  // open: gt, lt
  and and_4 (and_4_out, comparator_13_eq, comparator_14_eq);
  and and_5 (and_5_out, comparator_14_eq, comparator_15_eq);
  or or_10 (or_10_out, and_4_out, comparator_16_eq);
  Comparator #(.width(32)) comparator_17 (.a(32'h80000000), .b(x2), .eq(comparator_17_eq));  // open: gt, lt
  Comparator #(.width(32)) comparator_18 (.a(32'h1), .b(x), .eq(comparator_18_eq));  // open: gt, lt
  Comparator #(.width(32)) comparator_19 (.a(32'h40000000), .b(x2), .eq(\рядом_справа ));  // open: gt, lt
  Comparator #(.width(32)) comparator_20 (.a(32'h2), .b(x), .eq(\рядом_слева ));  // open: gt, lt
  or or_11 (or_11_out, comparator_17_eq, comparator_18_eq);
endmodule

module detect_hit___rocketka (
  input  Reset,
  input  \Вверх ,
  input  \Вниз ,
  input  [31:0] y,
  input  \рядом ,
  output [31:0] out,
  output \попал 
);

  wire _1, _2, _3, _4, and_22_out, and_31_out, bit_extender_5_out, bit_extender_6_out, bit_extender_7_out,
       bit_extender_8_out, bit_extender_9_out, bit_extender_10_out, bit_extender_11_out, bit_extender_12_out,
       bit_extender_13_out, bit_extender_14_out, bit_extender_15_out, bit_extender_16_out,
       bit_extender_17_out, bit_extender_18_out, bit_extender_19_out, bit_extender_20_out,
       bit_extender_21_out, bit_extender_22_out, bit_extender_23_out, bit_extender_24_out,
       bit_extender_25_out, bit_extender_26_out, bit_extender_27_out, bit_extender_28_out,
       bit_extender_29_out, bit_extender_30_out, bit_extender_31_out, bit_extender_32_out, clock_1_out,
       comparator_1_eq, comparator_2_eq, or_1_out, or_2_out;
  wire [4:0] adder_1_out, multiplexer_1_out, multiplexer_2_out, multiplexer_3_out, register_1_q,
       subtractor_1_out;
  wire [31:0] and_1_out, and_2_out, and_3_out, and_4_out, and_5_out, and_6_out, and_7_out, and_8_out,
       and_9_out, and_10_out, and_11_out, and_12_out, and_13_out, and_14_out, and_15_out, and_16_out,
       and_17_out, and_18_out, and_19_out, and_20_out, and_21_out, and_23_out, and_24_out, and_25_out,
       and_26_out, and_27_out, and_28_out, and_29_out, and_30_out, and_32_out, and_33_out, and_34_out,
       and_36_out, and_37_out, and_38_out, and_39_out, and_40_out, and_41_out, and_42_out, and_43_out,
       and_44_out, and_45_out, and_46_out, and_47_out, and_48_out, and_49_out, and_50_out, and_51_out,
       and_52_out, and_53_out, and_54_out, and_55_out, and_56_out, and_57_out, and_58_out, and_59_out,
       and_60_out, and_61_out, and_62_out, and_63_out, and_64_out, and_65_out, and_66_out, and_67_out,
       shifter_1_out, shifter_2_out, shifter_3_out, shifter_4_out, shifter_5_out, shifter_6_out,
       shifter_7_out, shifter_8_out, shifter_9_out, shifter_10_out, shifter_11_out, shifter_12_out,
       shifter_13_out, shifter_14_out, shifter_15_out, shifter_16_out, shifter_17_out, shifter_19_out,
       shifter_20_out, shifter_21_out, shifter_22_out, shifter_23_out, shifter_24_out, shifter_25_out,
       shifter_26_out, shifter_27_out, shifter_28_out, shifter_29_out, shifter_30_out, shifter_31_out,
       shifter_32_out;

  assign and_1_out = out & 32'h1;  // AND_Gate and_1, 32 bits wide
  Bit_Extender #(.in_width(32), .out_width(1)) bit_extender_1 (.in(and_4_out), .out(_1));
  Subtractor #(.width(5)) subtractor_1 (.a(register_1_q), .b(5'b00001), .out(subtractor_1_out));  // open: bin, bout
  Adder #(.width(5)) adder_1 (.a(register_1_q), .b(5'b00001), .out(adder_1_out));  // open: cin, cout
  assign and_2_out = out & 32'h4;  // AND_Gate and_2, 32 bits wide
  assign and_3_out = out & 32'h2;  // AND_Gate and_3, 32 bits wide
  assign and_4_out = and_1_out & y;  // AND_Gate and_4, 32 bits wide
  assign and_5_out = and_3_out & y;  // AND_Gate and_5, 32 bits wide
  Bit_Extender #(.in_width(32), .out_width(1)) bit_extender_2 (.in(shifter_2_out), .out(_2));
  assign and_6_out = out & 32'h8;  // AND_Gate and_6, 32 bits wide
  assign and_7_out = out & 32'h10;  // AND_Gate and_7, 32 bits wide
  assign and_8_out = and_2_out & y;  // AND_Gate and_8, 32 bits wide
  assign and_9_out = and_6_out & y;  // AND_Gate and_9, 32 bits wide
  Shifter #(.width(32), .shift("lr")) shifter_1 (.in(and_8_out), .\dist (5'b00010), .out(shifter_1_out));
  Shifter #(.width(32), .shift("lr")) shifter_2 (.in(and_5_out), .\dist (5'b00001), .out(shifter_2_out));
  Bit_Extender #(.in_width(32), .out_width(1)) bit_extender_3 (.in(shifter_1_out), .out(_3));
  Bit_Extender #(.in_width(32), .out_width(1)) bit_extender_4 (.in(shifter_4_out), .out(_4));
  assign and_10_out = out & 32'h40;  // AND_Gate and_10, 32 bits wide
  assign and_11_out = out & 32'h20;  // AND_Gate and_11, 32 bits wide
  assign and_12_out = and_7_out & y;  // AND_Gate and_12, 32 bits wide
  assign and_13_out = and_11_out & y;  // AND_Gate and_13, 32 bits wide
  Shifter #(.width(32), .shift("lr")) shifter_3 (.in(and_12_out), .\dist (5'b00100), .out(shifter_3_out));
  Shifter #(.width(32), .shift("lr")) shifter_4 (.in(and_9_out), .\dist (5'b00011), .out(shifter_4_out));
  Bit_Extender #(.in_width(32), .out_width(1)) bit_extender_5 (.in(shifter_3_out), .out(bit_extender_5_out));
  Comparator #(.width(5)) comparator_1 (.a(5'b01100), .b(adder_1_out), .eq(comparator_1_eq));  // open: gt, lt
  assign and_14_out = out & 32'h80;  // AND_Gate and_14, 32 bits wide
  assign and_15_out = out & 32'h100;  // AND_Gate and_15, 32 bits wide
  assign and_16_out = and_14_out & y;  // AND_Gate and_16, 32 bits wide
  assign and_17_out = and_10_out & y;  // AND_Gate and_17, 32 bits wide
  Shifter #(.width(32), .shift("lr")) shifter_5 (.in(and_17_out), .\dist (5'b00110), .out(shifter_5_out));
  Shifter #(.width(32), .shift("lr")) shifter_6 (.in(and_13_out), .\dist (5'b00101), .out(shifter_6_out));
  Bit_Extender #(.in_width(32), .out_width(1)) bit_extender_6 (.in(shifter_6_out), .out(bit_extender_6_out));
  Bit_Extender #(.in_width(32), .out_width(1)) bit_extender_7 (.in(shifter_5_out), .out(bit_extender_7_out));
  assign and_18_out = out & 32'h400;  // AND_Gate and_18, 32 bits wide
  assign and_19_out = out & 32'h200;  // AND_Gate and_19, 32 bits wide
  assign and_20_out = and_15_out & y;  // AND_Gate and_20, 32 bits wide
  assign and_21_out = and_19_out & y;  // AND_Gate and_21, 32 bits wide
  Shifter #(.width(32), .shift("lr")) shifter_7 (.in(and_20_out), .\dist (5'b01000), .out(shifter_7_out));
  Shifter #(.width(32), .shift("lr")) shifter_8 (.in(and_16_out), .\dist (5'b00111), .out(shifter_8_out));
  Bit_Extender #(.in_width(32), .out_width(1)) bit_extender_8 (.in(shifter_8_out), .out(bit_extender_8_out));
  Multiplexer #(.select(2), .width(5), .enable("false")) multiplexer_1 (
    .in0(register_1_q), .in1(subtractor_1_out), .in2(adder_1_out), .in3(register_1_q),
    .out(multiplexer_1_out), .sel({\Вверх , \Вниз }));
  and and_22 (and_22_out, \Вверх , comparator_1_eq);
  assign and_23_out = out & 32'h1000;  // AND_Gate and_23, 32 bits wide
  assign and_24_out = out & 32'h800;  // AND_Gate and_24, 32 bits wide
  assign and_25_out = and_18_out & y;  // AND_Gate and_25, 32 bits wide
  assign and_26_out = and_24_out & y;  // AND_Gate and_26, 32 bits wide
  Shifter #(.width(32), .shift("lr")) shifter_9 (.in(and_25_out), .\dist (5'b01010), .out(shifter_9_out));
  Shifter #(.width(32), .shift("lr")) shifter_10 (.in(and_21_out), .\dist (5'b01001), .out(shifter_10_out));
  Bit_Extender #(.in_width(32), .out_width(1)) bit_extender_9 (.in(shifter_7_out), .out(bit_extender_9_out));
  Bit_Extender #(.in_width(32), .out_width(1)) bit_extender_10 (.in(shifter_10_out), .out(bit_extender_10_out));
  Multiplexer #(.width(5), .enable("false")) multiplexer_2 (
    .in0(multiplexer_3_out), .in1(5'b01100), .out(multiplexer_2_out), .sel(Reset));
  Comparator #(.width(5)) comparator_2 (.a(5'b01111), .b(subtractor_1_out), .eq(comparator_2_eq));  // open: gt, lt
  assign and_27_out = out & 32'h2000;  // AND_Gate and_27, 32 bits wide
  assign and_28_out = out & 32'h4000;  // AND_Gate and_28, 32 bits wide
  assign and_29_out = and_23_out & y;  // AND_Gate and_29, 32 bits wide
  assign and_30_out = and_27_out & y;  // AND_Gate and_30, 32 bits wide
  Shifter #(.width(32), .shift("lr")) shifter_11 (.in(and_29_out), .\dist (5'b01100), .out(shifter_11_out));
  Shifter #(.width(32), .shift("lr")) shifter_12 (.in(and_26_out), .\dist (5'b01011), .out(shifter_12_out));
  Bit_Extender #(.in_width(32), .out_width(1)) bit_extender_11 (.in(shifter_12_out), .out(bit_extender_11_out));
  Bit_Extender #(.in_width(32), .out_width(1)) bit_extender_12 (.in(shifter_9_out), .out(bit_extender_12_out));
  or or_1 (or_1_out, _1, _2, _3, _4, bit_extender_5_out, bit_extender_6_out, bit_extender_7_out, bit_extender_8_out, bit_extender_9_out, bit_extender_10_out, bit_extender_12_out, bit_extender_11_out, bit_extender_13_out, bit_extender_14_out, bit_extender_16_out, bit_extender_19_out, bit_extender_15_out, bit_extender_17_out, bit_extender_18_out, bit_extender_20_out, bit_extender_21_out, bit_extender_22_out, bit_extender_24_out, bit_extender_23_out, bit_extender_25_out, bit_extender_26_out, bit_extender_27_out, bit_extender_29_out, bit_extender_30_out, bit_extender_28_out, bit_extender_32_out, bit_extender_31_out);
  and and_31 (and_31_out, \Вниз , comparator_2_eq);
  assign and_32_out = out & 32'h8000;  // AND_Gate and_32, 32 bits wide
  assign and_33_out = and_28_out & y;  // AND_Gate and_33, 32 bits wide
  assign and_34_out = and_32_out & y;  // AND_Gate and_34, 32 bits wide
  Shifter #(.width(32), .shift("lr")) shifter_13 (.in(and_33_out), .\dist (5'b01110), .out(shifter_13_out));
  Shifter #(.width(32), .shift("lr")) shifter_14 (.in(and_30_out), .\dist (5'b01101), .out(shifter_14_out));
  Bit_Extender #(.in_width(32), .out_width(1)) bit_extender_13 (.in(shifter_11_out), .out(bit_extender_13_out));
  and and_35 (\попал , or_1_out, \рядом );
  Multiplexer #(.width(5), .enable("false")) multiplexer_3 (
    .in0(multiplexer_1_out), .in1(register_1_q), .out(multiplexer_3_out), .sel(1'b0));
  Register #(.width(5)) register_1 (
    .D(multiplexer_2_out), .en(1'b1), .Q(register_1_q), .clk(clock_1_out));  // open: clr
  Clock clock_1 (.out(clock_1_out));
  or or_2 (or_2_out, and_31_out, and_22_out);
  assign and_36_out = out & 32'h20000;  // AND_Gate and_36, 32 bits wide
  assign and_37_out = out & 32'h10000;  // AND_Gate and_37, 32 bits wide
  assign and_38_out = and_37_out & y;  // AND_Gate and_38, 32 bits wide
  assign and_39_out = and_36_out & y;  // AND_Gate and_39, 32 bits wide
  Shifter #(.width(32), .shift("lr")) shifter_15 (.in(and_38_out), .\dist (5'b10000), .out(shifter_15_out));
  Shifter #(.width(32), .shift("lr")) shifter_16 (.in(and_34_out), .\dist (5'b01111), .out(shifter_16_out));
  Bit_Extender #(.in_width(32), .out_width(1)) bit_extender_14 (.in(shifter_14_out), .out(bit_extender_14_out));
  Bit_Extender #(.in_width(32), .out_width(1)) bit_extender_15 (.in(shifter_15_out), .out(bit_extender_15_out));
  assign and_40_out = out & 32'h40000;  // AND_Gate and_40, 32 bits wide
  assign and_41_out = out & 32'h80000;  // AND_Gate and_41, 32 bits wide
  assign and_42_out = and_41_out & y;  // AND_Gate and_42, 32 bits wide
  assign and_43_out = and_40_out & y;  // AND_Gate and_43, 32 bits wide
  Shifter #(.width(32), .shift("lr")) shifter_17 (.in(and_39_out), .\dist (5'b10001), .out(shifter_17_out));
  Bit_Extender #(.in_width(32), .out_width(1)) bit_extender_16 (.in(shifter_13_out), .out(bit_extender_16_out));
  Bit_Extender #(.in_width(32), .out_width(1)) bit_extender_17 (.in(shifter_17_out), .out(bit_extender_17_out));
  Bit_Extender #(.in_width(32), .out_width(1)) bit_extender_18 (.in(shifter_19_out), .out(bit_extender_18_out));
  Shifter #(.width(32)) shifter_18 (.in(32'hf), .\dist (register_1_q), .out(out));
  assign and_44_out = out & 32'h100000;  // AND_Gate and_44, 32 bits wide
  assign and_45_out = out & 32'h200000;  // AND_Gate and_45, 32 bits wide
  assign and_46_out = and_45_out & y;  // AND_Gate and_46, 32 bits wide
  assign and_47_out = and_44_out & y;  // AND_Gate and_47, 32 bits wide
  Shifter #(.width(32), .shift("lr")) shifter_19 (.in(and_43_out), .\dist (5'b10010), .out(shifter_19_out));
  Bit_Extender #(.in_width(32), .out_width(1)) bit_extender_19 (.in(shifter_16_out), .out(bit_extender_19_out));
  Bit_Extender #(.in_width(32), .out_width(1)) bit_extender_20 (.in(shifter_20_out), .out(bit_extender_20_out));
  assign and_48_out = out & 32'h800000;  // AND_Gate and_48, 32 bits wide
  assign and_49_out = out & 32'h400000;  // AND_Gate and_49, 32 bits wide
  assign and_50_out = and_48_out & y;  // AND_Gate and_50, 32 bits wide
  assign and_51_out = and_49_out & y;  // AND_Gate and_51, 32 bits wide
  Shifter #(.width(32), .shift("lr")) shifter_20 (.in(and_42_out), .\dist (5'b10011), .out(shifter_20_out));
  Bit_Extender #(.in_width(32), .out_width(1)) bit_extender_21 (.in(shifter_22_out), .out(bit_extender_21_out));
  assign and_52_out = out & 32'h2000000;  // AND_Gate and_52, 32 bits wide
  assign and_53_out = out & 32'h1000000;  // AND_Gate and_53, 32 bits wide
  assign and_54_out = and_53_out & y;  // AND_Gate and_54, 32 bits wide
  assign and_55_out = and_52_out & y;  // AND_Gate and_55, 32 bits wide
  Shifter #(.width(32), .shift("lr")) shifter_21 (.in(and_51_out), .\dist (5'b10110), .out(shifter_21_out));
  Shifter #(.width(32), .shift("lr")) shifter_22 (.in(and_47_out), .\dist (5'b10100), .out(shifter_22_out));
  Shifter #(.width(32), .shift("lr")) shifter_23 (.in(and_46_out), .\dist (5'b10101), .out(shifter_23_out));
  Bit_Extender #(.in_width(32), .out_width(1)) bit_extender_22 (.in(shifter_23_out), .out(bit_extender_22_out));
  assign and_56_out = out & 32'h4000000;  // AND_Gate and_56, 32 bits wide
  assign and_57_out = out & 32'h8000000;  // AND_Gate and_57, 32 bits wide
  assign and_58_out = and_57_out & y;  // AND_Gate and_58, 32 bits wide
  assign and_59_out = and_56_out & y;  // AND_Gate and_59, 32 bits wide
  Shifter #(.width(32), .shift("lr")) shifter_24 (.in(and_54_out), .\dist (5'b11000), .out(shifter_24_out));
  Shifter #(.width(32), .shift("lr")) shifter_25 (.in(and_50_out), .\dist (5'b10111), .out(shifter_25_out));
  Shifter #(.width(32), .shift("lr")) shifter_26 (.in(and_55_out), .\dist (5'b11001), .out(shifter_26_out));
  Bit_Extender #(.in_width(32), .out_width(1)) bit_extender_23 (.in(shifter_25_out), .out(bit_extender_23_out));
  Bit_Extender #(.in_width(32), .out_width(1)) bit_extender_24 (.in(shifter_21_out), .out(bit_extender_24_out));
  Bit_Extender #(.in_width(32), .out_width(1)) bit_extender_25 (.in(shifter_24_out), .out(bit_extender_25_out));
  assign and_60_out = out & 32'h20000000;  // AND_Gate and_60, 32 bits wide
  assign and_61_out = out & 32'h10000000;  // AND_Gate and_61, 32 bits wide
  assign and_62_out = and_61_out & y;  // AND_Gate and_62, 32 bits wide
  assign and_63_out = and_60_out & y;  // AND_Gate and_63, 32 bits wide
  Shifter #(.width(32), .shift("lr")) shifter_27 (.in(and_59_out), .\dist (5'b11010), .out(shifter_27_out));
  Shifter #(.width(32), .shift("lr")) shifter_28 (.in(and_58_out), .\dist (5'b11011), .out(shifter_28_out));
  Bit_Extender #(.in_width(32), .out_width(1)) bit_extender_26 (.in(shifter_26_out), .out(bit_extender_26_out));
  Bit_Extender #(.in_width(32), .out_width(1)) bit_extender_27 (.in(shifter_27_out), .out(bit_extender_27_out));
  assign and_64_out = out & 32'h80000000;  // AND_Gate and_64, 32 bits wide
  assign and_65_out = out & 32'h40000000;  // AND_Gate and_65, 32 bits wide
  assign and_66_out = and_64_out & y;  // AND_Gate and_66, 32 bits wide
  assign and_67_out = and_65_out & y;  // AND_Gate and_67, 32 bits wide
  Shifter #(.width(32), .shift("lr")) shifter_29 (.in(and_67_out), .\dist (5'b11110), .out(shifter_29_out));
  Shifter #(.width(32), .shift("lr")) shifter_30 (.in(and_62_out), .\dist (5'b11100), .out(shifter_30_out));
  Shifter #(.width(32), .shift("lr")) shifter_31 (.in(and_63_out), .\dist (5'b11101), .out(shifter_31_out));
  Bit_Extender #(.in_width(32), .out_width(1)) bit_extender_28 (.in(shifter_31_out), .out(bit_extender_28_out));
  Bit_Extender #(.in_width(32), .out_width(1)) bit_extender_29 (.in(shifter_28_out), .out(bit_extender_29_out));
  Bit_Extender #(.in_width(32), .out_width(1)) bit_extender_30 (.in(shifter_30_out), .out(bit_extender_30_out));
  Shifter #(.width(32), .shift("lr")) shifter_32 (.in(and_66_out), .\dist ({5{1'b1}}), .out(shifter_32_out));
  Bit_Extender #(.in_width(32), .out_width(1)) bit_extender_31 (.in(shifter_32_out), .out(bit_extender_31_out));
  Bit_Extender #(.in_width(32), .out_width(1)) bit_extender_32 (.in(shifter_29_out), .out(bit_extender_32_out));
endmodule

module x (
  input  \игра ,
  input  reset,
  input  hit,
  output vel_X,
  output [31:0] out,
  output [31:0] out_2
);

  wire and_1_out, clock_1_out, comparator_1_eq, comparator_2_eq, multiplexer_1_out, not_1_out, or_1_out,
       random_1_out;
  wire [0:0] xor_1_out;
  wire [4:0] bit_extender_2_out, bit_extender_3_out;
  wire [5:0] adder_2_out, multiplexer_2_out, register_2_q, subtractor_1_out;
  wire [31:0] adder_1_out, bit_extender_1_out, not_2_out, shifter_1_out, shifter_2_out;

  Comparator #(.width(6)) comparator_1 (.a({6{1'b1}}), .b(register_2_q), .eq(comparator_1_eq));  // open: gt, lt
  Comparator #(.width(6)) comparator_2 (.a({6{1'b0}}), .b(register_2_q), .eq(comparator_2_eq));  // open: gt, lt
  or or_1 (or_1_out, comparator_1_eq, comparator_2_eq, hit, reset);
  and and_1 (and_1_out, \игра , clock_1_out);
  Clock #(.highDuration(2), .lowDuration(2)) clock_1 (.out(clock_1_out));
  Random #(.width(1)) random_1 (.clk(and_1_out), .next(1'b1), .out(random_1_out), .clr(1'b0));
  assign bit_extender_1_out = {{31{1'b0}}, register_2_q[5]};  // Bit_Extender bit_extender_1
  Adder #(.width(32)) adder_1 (.a(bit_extender_1_out), .b({32{1'b1}}), .out(adder_1_out));  // open: cin, cout
  BitSelector #(.width(6), .group(5)) bitselector_1 ();  // open: in, out, sel
  Register #(.width(1)) register_1 (.D(multiplexer_1_out), .en(or_1_out), .Q(vel_X), .clk(and_1_out), .clr(1'b0));
  not not_1 (not_1_out, vel_X);
  Multiplexer #(.select(2), .enable("false")) multiplexer_1 (
    .in0(not_1_out), .in1(random_1_out), .in2(vel_X), .in3(vel_X), .out(multiplexer_1_out),
    .sel({1'b0, reset}));
  assign not_2_out = ~adder_1_out;  // NOT_Gate not_2, 32 bits wide
  Bit_Extender #(.in_width(6), .out_width(5)) bit_extender_2 (.in(register_2_q), .out(bit_extender_2_out));
  Bit_Extender #(.in_width(6), .out_width(5)) bit_extender_3 (.in(register_2_q), .out(bit_extender_3_out));
  xor xor_1 (xor_1_out[0], vel_X, or_1_out);
  Shifter #(.width(32)) shifter_1 (.in(32'h1), .\dist (bit_extender_2_out), .out(shifter_1_out));
  Shifter #(.width(32)) shifter_2 (.in(32'h1), .\dist (bit_extender_3_out), .out(shifter_2_out));
  Multiplexer #(.select(2), .width(6), .enable("false")) multiplexer_2 (
    .in0(adder_2_out), .in1(subtractor_1_out), .in2(6'b011111), .in3(6'b011111), .out(multiplexer_2_out),
    .sel({reset, xor_1_out[0]}));
  assign out = shifter_1_out & not_2_out;  // AND_Gate and_2, 32 bits wide
  assign out_2 = adder_1_out & shifter_2_out;  // AND_Gate and_3, 32 bits wide
  Register #(.width(6)) register_2 (.D(multiplexer_2_out), .en(1'b1), .Q(register_2_q), .clk(and_1_out));  // open: clr
  Adder #(.width(6)) adder_2 (.a(register_2_q), .b(6'b000001), .out(adder_2_out));  // open: cin, cout
  Subtractor #(.width(6)) subtractor_1 (.a(register_2_q), .b(6'b000001), .out(subtractor_1_out));  // open: bin, bout
endmodule

module y (
  input  \игра ,
  input  hit,
  input  reset,
  output vel_Y,
  output [31:0] out
);

  wire and_1_out, clock_1_out, comparator_1_eq, comparator_2_eq, multiplexer_1_out, not_1_out, or_1_out,
       random_2_out, register_1_q;
  wire [0:0] xor_1_out;
  wire [4:0] adder_1_out, multiplexer_2_out, random_1_out, register_3_q, subtractor_1_out;

  not not_1 (not_1_out, register_1_q);
  Multiplexer #(.select(2), .enable("false")) multiplexer_1 (
    .in0(not_1_out), .in1(random_2_out), .in2(register_1_q), .in3(register_1_q), .out(multiplexer_1_out),
    .sel({hit, reset}));
  Register #(.width(1)) register_1 (
    .D(multiplexer_1_out), .en(or_1_out), .Q(register_1_q), .clk(and_1_out));  // open: clr
  xor xor_1 (xor_1_out[0], or_1_out, vel_Y);
  or or_1 (or_1_out, comparator_2_eq, comparator_2_eq, comparator_1_eq);
  Random #(.width(5), .seed(1)) random_1 (.clk(and_1_out), .next(1'b1), .out(random_1_out), .clr(1'b0));
  Register #(.width(1)) register_2 (.D(multiplexer_1_out), .en(or_1_out), .Q(vel_Y), .clk(and_1_out), .clr(1'b0));
  Random #(.width(1), .seed(1)) random_2 (.clk(and_1_out), .next(1'b1), .out(random_2_out), .clr(1'b0));
  Clock #(.highDuration(2), .lowDuration(2)) clock_1 (.out(clock_1_out));
  and and_1 (and_1_out, clock_1_out, \игра );
  Multiplexer #(.select(2), .width(5), .enable("false")) multiplexer_2 (
    .in0(adder_1_out), .in1(subtractor_1_out), .in2(random_1_out), .in3(random_1_out),
    .out(multiplexer_2_out), .sel({reset, xor_1_out[0]}));
  Comparator #(.width(5)) comparator_1 (.a({5{1'b0}}), .b(register_3_q), .eq(comparator_1_eq));  // open: gt, lt
  Register #(.width(5)) register_3 (.D(multiplexer_2_out), .en(1'b1), .Q(register_3_q), .clk(and_1_out), .clr(1'b0));
  Comparator #(.width(5)) comparator_2 (.a({5{1'b1}}), .b(register_3_q), .eq(comparator_2_eq));  // open: gt, lt
  Random #(.width(2), .seed(2)) random_3 (.clk(vel_Y), .next(vel_Y), .clr(1'b0));  // open: out
  Subtractor #(.width(5)) subtractor_1 (.a(register_3_q), .b(5'b00001), .out(subtractor_1_out));  // open: bin, bout
  Adder #(.width(5)) adder_1 (.a(register_3_q), .b(5'b00001), .out(adder_1_out));  // open: cin, cout
  Shifter #(.width(32)) shifter_1 (.in(32'h1), .\dist (register_3_q), .out(out));
endmodule

module temp (
  input  [31:0] y,
  input  \рядом_справа ,
  input  upL,
  input  downL,
  input  downR,
  input  upR,
  input  \рядом_слева ,
  input  reset,
  output [31:0] outL,
  output [31:0] outR,
  output hit
);

  wire \detect_hit_rocketka_1_попал , \detect_hit_rocketka_2_попал ;

  detect_hit___rocketka detect_hit_rocketka_1 (
    .\Вверх (upL), .\Вниз (downL), .\рядом (\рядом_слева ), .out(outL), .Reset(reset), .y(y),
    .\попал (\detect_hit_rocketka_1_попал ));
  detect_hit___rocketka detect_hit_rocketka_2 (
    .\Вверх (upR), .\Вниз (downR), .\рядом (\рядом_справа ), .out(outR), .Reset(reset), .y(y),
    .\попал (\detect_hit_rocketka_2_попал ));
  or or_1 (hit, \detect_hit_rocketka_2_попал , \detect_hit_rocketka_1_попал );
  bot bot_1 ();  // open: outY, coord_X, vel_Y, coord_Y, vel_X, reset
endmodule

module bot (
  input  [31:0] coord_X,
  input  vel_Y,
  input  [31:0] coord_Y,
  input  vel_X,
  input  reset,
  output [31:0] outY
);

  wire cdm_8_1_p2, cdm_8_1_p5, cdm_8_1_p6, cdm_8_1_p7, cdm_8_1_p8, cdm_8_1_p9, cl, code,
       controlled_buffer_3_out, data, I_Osel, in_out_prime, mem, nand_1_out, not_1_out, not_2_out, not_3_out,
       not_4_out, not_5_out, OnCDM, pull_resistor_3_node, pull_resistor_4_node, pull_resistor_5_node, RAM,
       res, transistor_7_out, wrend;
  wire [1:0] counter_1_q;
  wire [3:0] I_Oadr;
  wire [4:0] bitfinder_1_index, bitfinder_2_index;
  wire [7:0] cdm_8_1_p4, cdm_8_1_p12, cdm_8_1_p13, cdm_8_1_p14, controlled_buffer_2_out, I_Odat,
       transistor_3_out;
  wire [7:4] transistor_2_out;

  Pull_Resistor pull_resistor_1 (.node(code));
  Pull_Resistor pull_resistor_2 (.node(data));
  Clock clock_1 (.out(cl));
  // Probe on cdm_8_1_p2
  // Probe on cdm_8_1_p4
  // Probe on cdm_8_1_p5
  Pull_Resistor pull_resistor_3 (.node(pull_resistor_3_node));
  Transistor #(.\type ("n")) transistor_1 (.in(cl), .out(pull_resistor_3_node), .gate(OnCDM));
  Shifter #(.width(32)) shifter_1 (.in(32'hf), .\dist (cdm_8_1_p4[4:0]), .out(outY));
  // Probe on cdm_8_1_p8
  // Probe on cdm_8_1_p7
  // Probe on cdm_8_1_p6
  and and_1 (I_Osel, not_1_out, cl, data);
  not not_1 (not_1_out, nand_1_out);
  and and_2 (RAM, nand_1_out, data);
  Transistor #(.\type ("n"), .width(8)) transistor_2 (.in(cdm_8_1_p12), .out({transistor_2_out, I_Oadr}), .gate(OnCDM));
  // CdM_8 cdm_8_1: pin names not known; wires that end beside it: pull_resistor_3_node, cdm_8_1_p2, res, cdm_8_1_p4, cdm_8_1_p5, cdm_8_1_p6, cdm_8_1_p7, cdm_8_1_p8, cdm_8_1_p9, mem, in_out_prime, cdm_8_1_p12, cdm_8_1_p13, cdm_8_1_p14
  Transistor #(.\type ("n"), .width(8)) transistor_3 (.in(cdm_8_1_p13), .out(transistor_3_out), .gate(OnCDM));
  Transistor #(.\type ("n"), .width(8)) transistor_4 (.in(controlled_buffer_2_out), .out(cdm_8_1_p14), .gate(OnCDM));
  nand nand_1 (nand_1_out, transistor_2_out[4], transistor_2_out[5], transistor_2_out[6], transistor_2_out[7]);
  Decoder decoder_1 (.out0(code), .out1(data), .sel(cdm_8_1_p9), .en(mem));
  assign I_Odat = not_2_out ? transistor_3_out : 8'bz;  // Controlled_Buffer controlled_buffer_1
  not not_2 (not_2_out, in_out_prime);
  assign controlled_buffer_2_out = in_out_prime ? I_Odat : 8'bz;  // Controlled_Buffer controlled_buffer_2
  Pull_Resistor pull_resistor_4 (.node(pull_resistor_4_node));
  Transistor #(.\type ("n")) transistor_5 (.in(code), .out(pull_resistor_4_node), .gate(OnCDM));
  Pull_Resistor #(.pull(1)) pull_resistor_5 (.node(pull_resistor_5_node));
  Transistor #(.\type ("n")) transistor_6 (.in(RAM), .out(pull_resistor_5_node), .gate(OnCDM));
  Pull_Resistor pull_resistor_6 (.node(I_Oadr[0]));
  Pull_Resistor pull_resistor_7 (.node(I_Oadr[1]));
  Pull_Resistor pull_resistor_8 (.node(I_Oadr[2]));
  Pull_Resistor pull_resistor_9 (.node(I_Oadr[3]));
  Pull_Resistor pull_resistor_10 (.node(transistor_2_out[4]));
  Pull_Resistor pull_resistor_11 (.node(transistor_2_out[5]));
  Pull_Resistor pull_resistor_12 (.node(transistor_2_out[6]));
  Pull_Resistor pull_resistor_13 (.node(transistor_2_out[7]));
  ROM rom_1 (.addr({transistor_2_out, I_Oadr}), .data(I_Odat), .sel(pull_resistor_4_node));
  RAM ram_1 (
    .addr({transistor_2_out, I_Oadr}), .data(I_Odat), .sel(pull_resistor_5_node), .clk(cl), .ld(OnCDM));  // open: clr
  Transistor #(.\type ("n")) transistor_7 (.in(in_out_prime), .out(transistor_7_out), .gate(OnCDM));
  Pull_Resistor pull_resistor_14 (.node(transistor_7_out));
  or or_1 (res, vel_X, reset);
  // Probe on {transistor_2_out, I_Oadr}
  // Probe on I_Odat
  Multiplexer #(.select(2), .width(8)) multiplexer_1 (
    .in0({3'b000, bitfinder_1_index}), .in1({3'b000, bitfinder_2_index}), .in2({{7{1'b0}}, vel_Y}),
    .in3({8{1'b0}}), .out(I_Odat), .sel(counter_1_q), .en(not_3_out));
  Multiplexer #(.select(2), .width(8)) multiplexer_2 (
    .in0(8'he4), .in1(8'he5), .in2(8'he3), .in3(8'hf0), .out({transistor_2_out, I_Oadr}), .sel(counter_1_q),
    .en(not_3_out));
  Counter #(.width(2), .max('h3), .ongoal("stay")) counter_1 (
    .load(1'b0), .count(1'b1), .Q(counter_1_q), .clk(cl), .clr(res));  // open: D, carry
  Comparator comparator_1 (.a(8'hf0), .b({transistor_2_out, I_Oadr}), .eq(wrend));  // open: gt, lt
  not not_3 (not_3_out, OnCDM);
  // Probe on counter_1_q
  // Probe on {3'b000, bitfinder_1_index}
  D_Flip_Flop d_ff_1 (.clk(cl), .D(wrend), .Q(OnCDM), .en(controlled_buffer_3_out));  // open: Qn, preset, reset
  assign controlled_buffer_3_out = not_4_out ? not_5_out : 1'bz;  // Controlled_Buffer controlled_buffer_3
  not not_4 (not_4_out, res);
  assign controlled_buffer_3_out = res ? res : 1'bz;  // Controlled_Buffer controlled_buffer_4
  Pull_Resistor pull_resistor_15 (.node(OnCDM));
  not not_5 (not_5_out, OnCDM);
  Pull_Resistor pull_resistor_16 (.node(res));
  BitFinder #(.width(32)) bitfinder_1 (.in(coord_X), .index(bitfinder_1_index));  // open: found
  BitFinder #(.width(32)) bitfinder_2 (.in(coord_Y), .index(bitfinder_2_index));  // open: found

  // Other names for the same wires on the sheet: rd_wr_prime = in_out_prime

  // Notes on the sheet:
  //   r2
  //   r1
  //   r0
  //   r3
  //   contents of rom_1 (hex, n*v repeats v):
  //   d0 e3 b3 8c b1 8c b2 d0 3e 85 11 f e0 f 85 19 5 e5 14 85 d3 20 77 ed 1b 37 d d4 198*0 1
  //   когда пытается записывать на 4 адрес можно включать cdm
endmodule

module menu (
  input  [6:0] \клавиатура ,
  output \пауза_игра ,
  output \меню_игра ,
  output _1_2_p,
  output \_1_2_p_выбор 
);

  wire _1_P_1___2_P_0_q, and_1_out, and_2_out, and_3_out, and_4_out, comparator_1_eq, comparator_2_eq,
       comparator_3_eq, comparator_4_eq, comparator_5_eq, comparator_6_eq, comparator_7_eq, nor_1_out,
       nor_2_out, not_7_out, not_8_out, or_1_out, or_2_out, \выход_out , \МЕНЮ_0___ИГРА_1_qn ;
  wire [6:0] not_1_out, not_2_out, not_3_out, not_4_out, not_5_out, not_6_out, not_9_out, not_10_out;

  Comparator #(.width(7)) comparator_1 (.a(\клавиатура ), .b({7{1'b0}}), .eq(comparator_1_eq));  // open: gt, lt
  assign not_1_out = ~\клавиатура ;  // NOT_Gate not_1, 7 bits wide
  assign not_2_out = ~not_1_out;  // NOT_Gate not_2, 7 bits wide
  assign not_3_out = ~not_2_out;  // NOT_Gate not_3, 7 bits wide
  assign not_4_out = ~not_9_out;  // NOT_Gate not_4, 7 bits wide
  assign not_5_out = ~not_3_out;  // NOT_Gate not_5, 7 bits wide
  assign not_6_out = ~not_10_out;  // NOT_Gate not_6, 7 bits wide
  Comparator #(.width(7)) comparator_2 (.a(not_5_out), .b(7'b0110001), .eq(comparator_2_eq));  // open: gt, lt
  not not_7 (not_7_out, not_8_out);
  not not_8 (not_8_out, comparator_1_eq);
  nor nor_1 (nor_1_out, comparator_2_eq, not_8_out);
  assign not_9_out = ~\клавиатура ;  // NOT_Gate not_9, 7 bits wide
  assign not_10_out = ~not_4_out;  // NOT_Gate not_10, 7 bits wide
  Comparator #(.width(7)) comparator_3 (.a(not_6_out), .b(7'b0110010), .eq(comparator_3_eq));  // open: gt, lt
  J_K_Flip_Flop _1_P_1___2_P_0 (
    .J(comparator_2_eq), .clk(not_7_out), .K(nor_1_out), .Q(_1_P_1___2_P_0_q));  // open: Qn, preset, en, reset
  Comparator #(.width(7)) comparator_4 (.a(\клавиатура ), .b(7'b0001010), .eq(comparator_4_eq));  // open: gt, lt
  J_K_Flip_Flop _1_P_0___2_P_1 (
    .J(comparator_3_eq), .clk(not_7_out), .K(nor_2_out), .Q(\_1_2_p_выбор ));  // open: Qn, preset, en, reset
  nor nor_2 (nor_2_out, comparator_3_eq, not_8_out);
  Comparator #(.width(7)) comparator_5 (.a(\клавиатура ), .b(7'b0100000), .eq(comparator_5_eq));  // open: gt, lt
  or or_1 (or_1_out, \_1_2_p_выбор , \меню_игра , _1_P_1___2_P_0_q);
  Comparator #(.width(7)) comparator_6 (.a(\клавиатура ), .b(7'b1000101), .eq(comparator_6_eq));  // open: gt, lt
  Comparator #(.width(7)) comparator_7 (.a(\клавиатура ), .b(7'b1100101), .eq(comparator_7_eq));  // open: gt, lt
  J_K_Flip_Flop \u_МЕНЮ_0___ИГРА_1  (
    .J(or_1_out), .clk(\выход_out ), .K(or_2_out), .Q(\меню_игра ), .Qn(\МЕНЮ_0___ИГРА_1_qn ), .en(or_1_out));  // open: preset, reset
  and and_1 (and_1_out, \меню_игра , comparator_6_eq, \пауза_игра );
  and and_2 (and_2_out, \меню_игра , comparator_7_eq, \пауза_игра );
  J_K_Flip_Flop \u_ПАУЗА_0___ИГРА_1  (
    .J(\меню_игра ), .clk(comparator_5_eq), .K(\меню_игра ), .Qn(\пауза_игра ));  // open: Q, preset, en, reset
  and and_3 (and_3_out, _1_P_1___2_P_0_q, \МЕНЮ_0___ИГРА_1_qn );
  and and_4 (and_4_out, \МЕНЮ_0___ИГРА_1_qn , \_1_2_p_выбор );
  or \u_выход  (\выход_out , and_1_out, comparator_4_eq, and_2_out);
  or or_2 (or_2_out, \пауза_игра , \выход_out );
  J_K_Flip_Flop _1_P_0___2_P_1_2 (
    .J(and_4_out), .clk(comparator_4_eq), .K(and_3_out), .Q(_1_2_p));  // open: Qn, preset, en, reset

  // Notes on the sheet:
  //   1
  //   ent
  //   2
  //   space
  //   E
  //   e
endmodule
module borders (
  input  \меню_игра ,
  output [3:0] bus_0,
  output [3:0] bus_0_2,
  output [3:0] bus_0_3,
  output [3:0] bus_0_4,
  output [3:0] bus_0_5,
  output [3:0] bus_0_6,
  output [3:0] bus_0_7,
  output [3:0] bus_0_8,
  output [3:0] bus_0_9,
  output [3:0] bus_0_10,
  output [3:0] bus_0_11,
  output [3:0] bus_0_12,
  output [3:0] bus_0_13,
  output [3:0] bus_0_14,
  output [3:0] bus_0_15,
  output [3:0] bus_0_16,
  output [3:0] bus_0_17,
  output [3:0] bus_0_18,
  output [3:0] bus_0_19,
  output [3:0] bus_0_20,
  output [3:0] bus_0_21,
  output [3:0] bus_0_22,
  output [3:0] bus_0_23,
  output [3:0] bus_0_24,
  output [3:0] bus_0_25,
  output [3:0] bus_0_26,
  output [3:0] bus_0_27,
  output [3:0] bus_0_28,
  output [3:0] bus_0_29,
  output [3:0] bus_0_30,
  output [3:0] bus_0_31,
  output [3:0] bus_0_32,
  output [3:0] bus_0_33,
  output [3:0] bus_0_34,
  output [3:0] bus_0_35,
  output [3:0] bus_0_36,
  output [3:0] bus_0_37,
  output [3:0] bus_0_38,
  output [3:0] bus_0_39,
  output [3:0] bus_0_40,
  output [3:0] bus_0_41,
  output [3:0] bus_0_42,
  output [3:0] bus_0_43,
  output [3:0] bus_0_44,
  output [3:0] bus_0_45,
  output [3:0] bus_0_46,
  output [3:0] bus_0_47,
  output [3:0] bus_0_48,
  output [3:0] bus_0_49,
  output [3:0] bus_0_50,
  output [3:0] bus_0_51,
  output [3:0] bus_0_52,
  output [3:0] bus_0_53,
  output [3:0] bus_0_54,
  output [3:0] bus_0_55,
  output [3:0] bus_0_56,
  output [3:0] bus_0_57,
  output [3:0] bus_0_58,
  output [3:0] bus_0_59,
  output [3:0] bus_0_60,
  output [3:0] bus_0_61,
  output [3:0] bus_0_62,
  output [3:0] bus_0_63,
  output [3:0] bus_0_64,
  output [3:0] bus_0_65,
  output [3:0] bus_0_66,
  output [3:0] bus_0_67,
  output [3:0] bus_0_68,
  output [3:0] bus_0_69,
  output [3:0] bus_0_70,
  output [3:0] bus_0_71,
  output [3:0] bus_0_72,
  output [3:0] bus_0_73,
  output [3:0] bus_0_74,
  output [3:0] bus_0_75,
  output [3:0] bus_0_76,
  output [3:0] bus_0_77,
  output [3:0] bus_0_78,
  output [3:0] bus_0_79,
  output [3:0] bus_0_80,
  output [3:0] bus_0_81,
  output [3:0] bus_0_82,
  output [3:0] bus_0_83,
  output [3:0] bus_0_84,
  output [3:0] bus_0_85,
  output [3:0] bus_0_86,
  output [3:0] bus_0_87,
  output [3:0] bus_0_88,
  output [3:0] bus_0_89,
  output [3:0] bus_0_90,
  output [3:0] bus_0_91,
  output [3:0] bus_0_92,
  output [3:0] bus_0_93,
  output [3:0] bus_0_94,
  output [3:0] bus_0_95,
  output [3:0] bus_0_96,
  output [3:0] bus_0_97,
  output [3:0] bus_0_98,
  output [3:0] bus_0_99,
  output [3:0] bus_0_100,
  output [3:0] bus_0_101,
  output [3:0] bus_0_102,
  output [3:0] bus_0_103,
  output [3:0] bus_0_104,
  output [3:0] bus_0_105,
  output [3:0] bus_0_106,
  output [3:0] bus_0_107,
  output [3:0] bus_0_108,
  output [3:0] bus_0_109,
  output [3:0] bus_0_110,
  output [3:0] bus_0_111,
  output [3:0] bus_0_112,
  output [3:0] bus_0_113,
  output [3:0] bus_0_114,
  output [3:0] bus_0_115,
  output [3:0] bus_0_116,
  output [3:0] bus_0_117,
  output [3:0] bus_0_118,
  output [3:0] bus_0_119,
  output [3:0] bus_0_120,
  output [3:0] bus_0_121,
  output [3:0] bus_0_122,
  output [3:0] bus_0_123,
  output [3:0] bus_0_124,
  output [3:0] bus_0_125,
  output [3:0] bus_0_126,
  output [3:0] bus_0_127,
  output [3:0] bus_0_128,
  output [3:0] bus_0_129,
  output [3:0] bus_0_130,
  output [3:0] bus_0_131,
  output [3:0] bus_0_132,
  output [3:0] bus_0_133,
  output [3:0] bus_0_134,
  output [3:0] bus_0_135,
  output [3:0] bus_0_136,
  output [3:0] bus_0_137,
  output [3:0] bus_0_138,
  output [3:0] bus_0_139,
  output [3:0] bus_0_140,
  output [3:0] bus_0_141,
  output [3:0] bus_0_142,
  output [3:0] bus_0_143,
  output [3:0] bus_0_144,
  output [3:0] bus_0_145,
  output [3:0] bus_0_146,
  output [3:0] bus_0_147,
  output [3:0] bus_0_148,
  output [3:0] bus_0_149,
  output [3:0] bus_0_150,
  output [3:0] bus_0_151,
  output [3:0] bus_0_152,
  output [3:0] bus_0_153,
  output [3:0] bus_0_154,
  output [3:0] bus_0_155,
  output [3:0] bus_0_156,
  output [3:0] bus_0_157,
  output [3:0] bus_0_158,
  output [3:0] bus_0_159,
  output [3:0] bus_0_160,
  output [3:0] bus_0_161,
  output [3:0] bus_0_162,
  output [3:0] bus_0_163,
  output [3:0] bus_0_164,
  output [3:0] bus_0_165,
  output [3:0] bus_0_166,
  output [3:0] bus_0_167,
  output [3:0] bus_0_168,
  output [3:0] bus_0_169,
  output [3:0] bus_0_170,
  output [3:0] bus_0_171,
  output [3:0] bus_0_172,
  output [3:0] bus_0_173,
  output [3:0] bus_0_174,
  output [3:0] bus_0_175,
  output [3:0] bus_0_176,
  output [3:0] bus_0_177,
  output [3:0] bus_0_178,
  output [3:0] bus_0_179,
  output [3:0] bus_0_180,
  output [3:0] bus_0_181,
  output [3:0] bus_0_182,
  output [3:0] bus_0_183,
  output [3:0] bus_0_184,
  output [3:0] bus_0_185,
  output [3:0] bus_0_186,
  output [3:0] bus_0_187,
  output [3:0] bus_0_188,
  output [3:0] bus_0_189,
  output [3:0] bus_0_190,
  output [3:0] bus_0_191,
  output [3:0] bus_0_192,
  output [3:0] bus_0_193,
  output [3:0] bus_0_194,
  output [3:0] bus_0_195,
  output [3:0] bus_0_196,
  output [3:0] bus_0_197,
  output [3:0] bus_0_198,
  output [3:0] bus_0_199,
  output [3:0] bus_0_200,
  output [3:0] bus_0_201,
  output [3:0] bus_0_202,
  output [3:0] bus_0_203,
  output [3:0] bus_0_204,
  output [3:0] bus_0_205,
  output [3:0] bus_0_206,
  output [3:0] bus_0_207,
  output [3:0] bus_0_208
);

  wire not_1_out;

  not not_1 (not_1_out, \меню_игра );
  b11 b11_1 (.bus_0(not_1_out), .bus_0_2(bus_0), .bus_0_3(bus_0_19), .bus_0_4(bus_0_37), .bus_0_5(bus_0_55));
  b2_2 b2_2_1 (.bus_0(not_1_out), .bus_0_2(bus_0_73), .bus_0_3(bus_0_75), .bus_0_4(bus_0_77), .bus_0_5(bus_0_79));
  b2_2 b2_2_2 (.bus_0(not_1_out), .bus_0_2(bus_0_81), .bus_0_3(bus_0_83), .bus_0_4(bus_0_85), .bus_0_5(bus_0_87));
  b2_2 b2_2_3 (.bus_0(not_1_out), .bus_0_2(bus_0_89), .bus_0_3(bus_0_91), .bus_0_4(bus_0_93), .bus_0_5(bus_0_95));
  b2_2 b2_2_4 (.bus_0(not_1_out), .bus_0_2(bus_0_97), .bus_0_3(bus_0_99), .bus_0_4(bus_0_101), .bus_0_5(bus_0_103));
  b2_2 b2_2_5 (.bus_0(not_1_out), .bus_0_2(bus_0_105), .bus_0_3(bus_0_107), .bus_0_4(bus_0_109), .bus_0_5(bus_0_111));
  b2_2 b2_2_6 (.bus_0(not_1_out), .bus_0_2(bus_0_113), .bus_0_3(bus_0_115), .bus_0_4(bus_0_117), .bus_0_5(bus_0_119));
  b2_2 b2_2_7 (.bus_0(not_1_out), .bus_0_2(bus_0_121), .bus_0_3(bus_0_123), .bus_0_4(bus_0_125), .bus_0_5(bus_0_127));
  b2_2 b2_2_8 (.bus_0(not_1_out), .bus_0_2(bus_0_129), .bus_0_3(bus_0_131), .bus_0_4(bus_0_133), .bus_0_5(bus_0_135));
  b10_1 b10_1_1 (.bus_0(not_1_out), .bus_0_2(bus_0_137), .bus_0_3(bus_0_155), .bus_0_4(bus_0_173), .bus_0_5(bus_0_191));
  b12 b12_1 (.bus_0(not_1_out), .bus_0_2(bus_0_2), .bus_0_3(bus_0_20), .bus_0_4(bus_0_38), .bus_0_5(bus_0_56));
  b10_2 b10_2_1 (.bus_0(not_1_out), .bus_0_2(bus_0_138), .bus_0_3(bus_0_156), .bus_0_4(bus_0_174), .bus_0_5(bus_0_192));
  b12 b12_2 (.bus_0(not_1_out), .bus_0_2(bus_0_3), .bus_0_3(bus_0_21), .bus_0_4(bus_0_39), .bus_0_5(bus_0_57));
  b10_2 b10_2_2 (.bus_0(not_1_out), .bus_0_2(bus_0_139), .bus_0_3(bus_0_157), .bus_0_4(bus_0_175), .bus_0_5(bus_0_193));
  b12 b12_3 (.bus_0(not_1_out), .bus_0_2(bus_0_4), .bus_0_3(bus_0_22), .bus_0_4(bus_0_40), .bus_0_5(bus_0_58));
  b10_2 b10_2_3 (.bus_0(not_1_out), .bus_0_2(bus_0_140), .bus_0_3(bus_0_158), .bus_0_4(bus_0_176), .bus_0_5(bus_0_194));
  b12 b12_4 (.bus_0(not_1_out), .bus_0_2(bus_0_5), .bus_0_3(bus_0_23), .bus_0_4(bus_0_41), .bus_0_5(bus_0_59));
  b12 b12_5 (.bus_0(not_1_out), .bus_0_2(bus_0_6), .bus_0_3(bus_0_24), .bus_0_4(bus_0_42), .bus_0_5(bus_0_60));
  b10_2 b10_2_4 (.bus_0(not_1_out), .bus_0_2(bus_0_141), .bus_0_3(bus_0_159), .bus_0_4(bus_0_177), .bus_0_5(bus_0_195));
  b10_2 b10_2_5 (.bus_0(not_1_out), .bus_0_2(bus_0_142), .bus_0_3(bus_0_160), .bus_0_4(bus_0_178), .bus_0_5(bus_0_196));
  b12 b12_6 (.bus_0(not_1_out), .bus_0_2(bus_0_7), .bus_0_3(bus_0_25), .bus_0_4(bus_0_43), .bus_0_5(bus_0_61));
  b10_2 b10_2_6 (.bus_0(not_1_out), .bus_0_2(bus_0_143), .bus_0_3(bus_0_161), .bus_0_4(bus_0_179), .bus_0_5(bus_0_197));
  b12 b12_7 (.bus_0(not_1_out), .bus_0_2(bus_0_8), .bus_0_3(bus_0_26), .bus_0_4(bus_0_44), .bus_0_5(bus_0_62));
  b10_2 b10_2_7 (.bus_0(not_1_out), .bus_0_2(bus_0_144), .bus_0_3(bus_0_162), .bus_0_4(bus_0_180), .bus_0_5(bus_0_198));
  b12 b12_8 (.bus_0(not_1_out), .bus_0_2(bus_0_9), .bus_0_3(bus_0_27), .bus_0_4(bus_0_45), .bus_0_5(bus_0_63));
  b10_2 b10_2_8 (.bus_0(not_1_out), .bus_0_2(bus_0_145), .bus_0_3(bus_0_163), .bus_0_4(bus_0_181), .bus_0_5(bus_0_199));
  b10_2 b10_2_9 (.bus_0(not_1_out), .bus_0_2(bus_0_146), .bus_0_3(bus_0_164), .bus_0_4(bus_0_182), .bus_0_5(bus_0_200));
  b12 b12_9 (.bus_0(not_1_out), .bus_0_2(bus_0_10), .bus_0_3(bus_0_28), .bus_0_4(bus_0_46), .bus_0_5(bus_0_64));
  b12 b12_10 (.bus_0(not_1_out), .bus_0_2(bus_0_11), .bus_0_3(bus_0_29), .bus_0_4(bus_0_47), .bus_0_5(bus_0_65));
  b10_2 b10_2_10 (
    .bus_0(not_1_out), .bus_0_2(bus_0_147), .bus_0_3(bus_0_165), .bus_0_4(bus_0_183), .bus_0_5(bus_0_201));
  b12 b12_11 (.bus_0(not_1_out), .bus_0_2(bus_0_12), .bus_0_3(bus_0_30), .bus_0_4(bus_0_48), .bus_0_5(bus_0_66));
  b10_2 b10_2_11 (
    .bus_0(not_1_out), .bus_0_2(bus_0_148), .bus_0_3(bus_0_166), .bus_0_4(bus_0_184), .bus_0_5(bus_0_202));
  b1_13 b1_13_1 (.bus_0(not_1_out), .bus_0_2(bus_0_13), .bus_0_3(bus_0_31), .bus_0_4(bus_0_49), .bus_0_5(bus_0_67));
  b10_2 b10_2_12 (
    .bus_0(not_1_out), .bus_0_2(bus_0_150), .bus_0_3(bus_0_168), .bus_0_4(bus_0_186), .bus_0_5(bus_0_204));
  b10_13 b10_13_1 (
    .bus_0(not_1_out), .bus_0_2(bus_0_149), .bus_0_3(bus_0_167), .bus_0_4(bus_0_185), .bus_0_5(bus_0_203));
  b12 b12_12 (.bus_0(not_1_out), .bus_0_2(bus_0_14), .bus_0_3(bus_0_32), .bus_0_4(bus_0_50), .bus_0_5(bus_0_68));
  b10_2 b10_2_13 (
    .bus_0(not_1_out), .bus_0_2(bus_0_151), .bus_0_3(bus_0_169), .bus_0_4(bus_0_187), .bus_0_5(bus_0_205));
  b12 b12_13 (.bus_0(not_1_out), .bus_0_2(bus_0_15), .bus_0_3(bus_0_33), .bus_0_4(bus_0_51), .bus_0_5(bus_0_69));
  b12 b12_14 (.bus_0(not_1_out), .bus_0_2(bus_0_16), .bus_0_3(bus_0_34), .bus_0_4(bus_0_52), .bus_0_5(bus_0_70));
  b10_2 b10_2_14 (
    .bus_0(not_1_out), .bus_0_2(bus_0_152), .bus_0_3(bus_0_170), .bus_0_4(bus_0_188), .bus_0_5(bus_0_206));
  b12 b12_15 (.bus_0(not_1_out), .bus_0_2(bus_0_17), .bus_0_3(bus_0_35), .bus_0_4(bus_0_53), .bus_0_5(bus_0_71));
  b10_2 b10_2_15 (
    .bus_0(not_1_out), .bus_0_2(bus_0_153), .bus_0_3(bus_0_171), .bus_0_4(bus_0_189), .bus_0_5(bus_0_207));
  b1_18 b1_18_1 (.bus_0(not_1_out), .bus_0_2(bus_0_18), .bus_0_3(bus_0_36), .bus_0_4(bus_0_54), .bus_0_5(bus_0_72));
  b2_18 b2_18_1 (.bus_0(not_1_out), .bus_0_2(bus_0_74), .bus_0_3(bus_0_76), .bus_0_4(bus_0_78), .bus_0_5(bus_0_80));
  b2_18 b2_18_2 (.bus_0(not_1_out), .bus_0_2(bus_0_82), .bus_0_3(bus_0_84), .bus_0_4(bus_0_86), .bus_0_5(bus_0_88));
  b2_18 b2_18_3 (.bus_0(not_1_out), .bus_0_2(bus_0_90), .bus_0_3(bus_0_92), .bus_0_4(bus_0_94), .bus_0_5(bus_0_96));
  b2_18 b2_18_4 (.bus_0(not_1_out), .bus_0_2(bus_0_98), .bus_0_3(bus_0_100), .bus_0_4(bus_0_102), .bus_0_5(bus_0_104));
  b2_18 b2_18_5 (.bus_0(not_1_out), .bus_0_2(bus_0_106), .bus_0_3(bus_0_108), .bus_0_4(bus_0_110), .bus_0_5(bus_0_112));
  b2_18 b2_18_6 (.bus_0(not_1_out), .bus_0_2(bus_0_114), .bus_0_3(bus_0_116), .bus_0_4(bus_0_118), .bus_0_5(bus_0_120));
  b2_18 b2_18_7 (.bus_0(not_1_out), .bus_0_2(bus_0_122), .bus_0_3(bus_0_124), .bus_0_4(bus_0_126), .bus_0_5(bus_0_128));
  b2_18 b2_18_8 (.bus_0(not_1_out), .bus_0_2(bus_0_130), .bus_0_3(bus_0_132), .bus_0_4(bus_0_134), .bus_0_5(bus_0_136));
  b10_18 b10_18_1 (
    .bus_0(not_1_out), .bus_0_2(bus_0_154), .bus_0_3(bus_0_172), .bus_0_4(bus_0_190), .bus_0_5(bus_0_208));
endmodule

module b11 (
  input  bus_0,
  output [3:0] bus_0_2,
  output [3:0] bus_0_3,
  output [3:0] bus_0_4,
  output [3:0] bus_0_5
);

  Multiplexer #(.width(4)) multiplexer_1 (.in0(4'b1111), .in1(4'b0000), .out(bus_0_2), .sel(bus_0));  // open: en
  Multiplexer #(.width(4)) multiplexer_2 (.in0(4'b1000), .in1(4'b0111), .out(bus_0_3), .sel(bus_0));  // open: en
  Multiplexer #(.width(4)) multiplexer_3 (.in0(4'b1000), .in1(4'b0100), .out(bus_0_4), .sel(bus_0));  // open: en
  Multiplexer #(.width(4)) multiplexer_4 (.in0(4'b1001), .in1(4'b0100), .out(bus_0_5), .sel(bus_0));  // open: en
endmodule

module b12 (
  input  bus_0,
  output [3:0] bus_0_2,
  output [3:0] bus_0_3,
  output [3:0] bus_0_4,
  output [3:0] bus_0_5
);

  Multiplexer #(.width(4)) multiplexer_1 (.in0(4'b1001), .in1(4'b0100), .out(bus_0_2), .sel(bus_0));  // open: en
  Multiplexer #(.width(4)) multiplexer_2 (.in0(4'b1001), .in1(4'b0100), .out(bus_0_3), .sel(bus_0));  // open: en
  Multiplexer #(.width(4)) multiplexer_3 (.in0(4'b1001), .in1(4'b0100), .out(bus_0_4), .sel(bus_0));  // open: en
  Multiplexer #(.width(4)) multiplexer_4 (.in0(4'b1001), .in1(4'b0100), .out(bus_0_5), .sel(bus_0));  // open: en
endmodule

module b1_18 (
  input  bus_0,
  output [3:0] bus_0_2,
  output [3:0] bus_0_3,
  output [3:0] bus_0_4,
  output [3:0] bus_0_5
);

  Multiplexer #(.width(4)) multiplexer_1 (.in0(4'b1001), .in1(4'b0100), .out(bus_0_2), .sel(bus_0));  // open: en
  Multiplexer #(.width(4)) multiplexer_2 (.in0(4'b1000), .in1(4'b0100), .out(bus_0_3), .sel(bus_0));  // open: en
  Multiplexer #(.width(4)) multiplexer_3 (.in0(4'b1000), .in1(4'b0111), .out(bus_0_4), .sel(bus_0));  // open: en
  Multiplexer #(.width(4)) multiplexer_4 (.in0(4'b1111), .in1(4'b0000), .out(bus_0_5), .sel(bus_0));  // open: en
endmodule

module b1_13 (
  input  bus_0,
  output [3:0] bus_0_2,
  output [3:0] bus_0_3,
  output [3:0] bus_0_4,
  output [3:0] bus_0_5
);

  Multiplexer #(.width(4)) multiplexer_1 (.in0(4'b1001), .in1(4'b0111), .out(bus_0_2), .sel(bus_0));  // open: en
  Multiplexer #(.width(4)) multiplexer_2 (.in0(4'b1001), .in1(4'b0100), .out(bus_0_3), .sel(bus_0));  // open: en
  Multiplexer #(.width(4)) multiplexer_3 (.in0(4'b1001), .in1(4'b0100), .out(bus_0_4), .sel(bus_0));  // open: en
  Multiplexer #(.width(4)) multiplexer_4 (.in0(4'b1001), .in1(4'b0100), .out(bus_0_5), .sel(bus_0));  // open: en
endmodule

module b2_2 (
  input  bus_0,
  output [3:0] bus_0_2,
  output [3:0] bus_0_3,
  output [3:0] bus_0_4,
  output [3:0] bus_0_5
);

  Multiplexer #(.width(4)) multiplexer_1 (.in0(4'b1111), .in1(4'b0000), .out(bus_0_2), .sel(bus_0));  // open: en
  Multiplexer #(.width(4)) multiplexer_2 (.in0(4'b0000), .in1(4'b1111), .out(bus_0_3), .sel(bus_0));  // open: en
  Multiplexer #(.width(4)) multiplexer_3 (.in0(4'b0000), .in1(4'b0000), .out(bus_0_4), .sel(bus_0));  // open: en
  Multiplexer #(.width(4)) multiplexer_4 (.in0(4'b1111), .in1(4'b0000), .out(bus_0_5), .sel(bus_0));  // open: en
endmodule

module b2_18 (
  input  bus_0,
  output [3:0] bus_0_2,
  output [3:0] bus_0_3,
  output [3:0] bus_0_4,
  output [3:0] bus_0_5
);

  Multiplexer #(.width(4)) multiplexer_1 (.in0(4'b1111), .in1(4'b0000), .out(bus_0_2), .sel(bus_0));  // open: en
  Multiplexer #(.width(4)) multiplexer_2 (.in0(4'b0000), .in1(4'b0000), .out(bus_0_3), .sel(bus_0));  // open: en
  Multiplexer #(.width(4)) multiplexer_3 (.in0(4'b0000), .in1(4'b1111), .out(bus_0_4), .sel(bus_0));  // open: en
  Multiplexer #(.width(4)) multiplexer_4 (.in0(4'b1111), .in1(4'b0000), .out(bus_0_5), .sel(bus_0));  // open: en
endmodule

module b10_1 (
  input  bus_0,
  output [3:0] bus_0_2,
  output [3:0] bus_0_3,
  output [3:0] bus_0_4,
  output [3:0] bus_0_5
);

  Multiplexer #(.width(4)) multiplexer_1 (.in0(4'b1111), .in1(4'b0000), .out(bus_0_2), .sel(bus_0));  // open: en
  Multiplexer #(.width(4)) multiplexer_2 (.in0(4'b0001), .in1(4'b1110), .out(bus_0_3), .sel(bus_0));  // open: en
  Multiplexer #(.width(4)) multiplexer_3 (.in0(4'b0001), .in1(4'b0010), .out(bus_0_4), .sel(bus_0));  // open: en
  Multiplexer #(.width(4)) multiplexer_4 (.in0(4'b1001), .in1(4'b0010), .out(bus_0_5), .sel(bus_0));  // open: en
endmodule

module b10_2 (
  input  bus_0,
  output [3:0] bus_0_2,
  output [3:0] bus_0_3,
  output [3:0] bus_0_4,
  output [3:0] bus_0_5
);

  Multiplexer #(.width(4)) multiplexer_1 (.in0(4'b1001), .in1(4'b0010), .out(bus_0_2), .sel(bus_0));  // open: en
  Multiplexer #(.width(4)) multiplexer_2 (.in0(4'b1001), .in1(4'b0010), .out(bus_0_3), .sel(bus_0));  // open: en
  Multiplexer #(.width(4)) multiplexer_3 (.in0(4'b1001), .in1(4'b0010), .out(bus_0_4), .sel(bus_0));  // open: en
  Multiplexer #(.width(4)) multiplexer_4 (.in0(4'b1001), .in1(4'b0010), .out(bus_0_5), .sel(bus_0));  // open: en
endmodule

module b10_13 (
  input  bus_0,
  output [3:0] bus_0_2,
  output [3:0] bus_0_3,
  output [3:0] bus_0_4,
  output [3:0] bus_0_5
);

  Multiplexer #(.width(4)) multiplexer_1 (.in0(4'b1001), .in1(4'b1110), .out(bus_0_2), .sel(bus_0));  // open: en
  Multiplexer #(.width(4)) multiplexer_2 (.in0(4'b1001), .in1(4'b0010), .out(bus_0_3), .sel(bus_0));  // open: en
  Multiplexer #(.width(4)) multiplexer_3 (.in0(4'b1001), .in1(4'b0010), .out(bus_0_4), .sel(bus_0));  // open: en
  Multiplexer #(.width(4)) multiplexer_4 (.in0(4'b1001), .in1(4'b0010), .out(bus_0_5), .sel(bus_0));  // open: en
endmodule

module b10_18 (
  input  bus_0,
  output [3:0] bus_0_2,
  output [3:0] bus_0_3,
  output [3:0] bus_0_4,
  output [3:0] bus_0_5
);

  Multiplexer #(.width(4)) multiplexer_1 (.in0(4'b1001), .in1(4'b0010), .out(bus_0_2), .sel(bus_0));  // open: en
  Multiplexer #(.width(4)) multiplexer_2 (.in0(4'b0001), .in1(4'b0010), .out(bus_0_3), .sel(bus_0));  // open: en
  Multiplexer #(.width(4)) multiplexer_3 (.in0(4'b0001), .in1(4'b1110), .out(bus_0_4), .sel(bus_0));  // open: en
  Multiplexer #(.width(4)) multiplexer_4 (.in0(4'b1111), .in1(4'b0000), .out(bus_0_5), .sel(bus_0));  // open: en
endmodule

module bigc (
  input  restart,
  input  \рядом_справа ,
  input  [6:0] \клавиатура ,
  input  \рядом_слева ,
  output [31:0] x1,
  output [31:0] x2,
  output [31:0] y,
  output [31:0] out_L,
  output [31:0] out_R
);

  wire _1_2p, and_1_out, clock_1_out, comparator_1_eq, comparator_2_eq, comparator_3_eq, comparator_4_eq,
       comparator_5_eq, comparator_6_eq, comparator_7_eq, comparator_8_eq, comparator_9_gt, comparator_9_lt,
       downL, downRp, hit, j_k_ff_1_qn, j_k_ff_2_qn, j_k_ff_3_qn, j_k_ff_4_qn, \menu_1_меню_игра ,
       \menu_1_пауза_игра , multiplexer_1_out, multiplexer_2_out, not_1_out, or_1_out, or_2_out, or_3_out,
       or_4_out, upL, upRp, vel_X, vel_Y;
  wire [1:0] counter_1_q, counter_2_q, counter_3_q, counter_4_q;
  wire [31:0] botres;

  Comparator #(.width(7)) comparator_1 (.a(\клавиатура ), .b(7'b1110111), .eq(comparator_1_eq));  // open: gt, lt
  Comparator #(.width(7)) comparator_2 (.a(\клавиатура ), .b(7'b1010111), .eq(comparator_2_eq));  // open: gt, lt
  Comparator #(.width(7)) comparator_3 (.a(\клавиатура ), .b(7'b1110011), .eq(comparator_3_eq));  // open: gt, lt
  Comparator #(.width(7)) comparator_4 (.a(\клавиатура ), .b(7'b1010011), .eq(comparator_4_eq));  // open: gt, lt
  or or_1 (or_1_out, comparator_1_eq, comparator_2_eq);
  or or_2 (or_2_out, comparator_3_eq, comparator_4_eq);
  J_K_Flip_Flop j_k_ff_1 (
    .J(or_1_out), .clk(or_1_out), .K(or_1_out), .Q(upL), .Qn(j_k_ff_1_qn), .reset(counter_1_q[1]));  // open: preset, en
  Counter #(.width(2), .max('h3)) counter_1 (
    .count(upL), .Q(counter_1_q), .clk(clock_1_out), .clr(j_k_ff_1_qn));  // open: load, D, carry
  J_K_Flip_Flop j_k_ff_2 (
    .J(or_2_out), .clk(or_2_out), .K(or_2_out), .Q(downL), .Qn(j_k_ff_2_qn), .reset(counter_2_q[1]));  // open: preset, en
  Counter #(.width(2), .max('h3)) counter_2 (
    .count(downL), .Q(counter_2_q), .clk(clock_1_out), .clr(j_k_ff_2_qn));  // open: load, D, carry
  bot bot_1 (.outY(botres), .coord_X(x1), .vel_Y(vel_Y), .coord_Y(y), .vel_X(vel_X), .reset(restart));
  Comparator #(.width(7)) comparator_5 (.a(\клавиатура ), .b(7'b1101001), .eq(comparator_5_eq));  // open: gt, lt
  Comparator #(.width(7)) comparator_6 (.a(\клавиатура ), .b(7'b1001001), .eq(comparator_6_eq));  // open: gt, lt
  Comparator #(.width(7)) comparator_7 (.a(\клавиатура ), .b(7'b1101011), .eq(comparator_7_eq));  // open: gt, lt
  Comparator #(.width(7)) comparator_8 (.a(\клавиатура ), .b(7'b1001011), .eq(comparator_8_eq));  // open: gt, lt
  Clock clock_1 (.out(clock_1_out));
  menu menu_1 (
    .\клавиатура (\клавиатура ), .\пауза_игра (\menu_1_пауза_игра ), .\меню_игра (\menu_1_меню_игра ),
    ._1_2_p(_1_2p));  // open: _1_2_p_выбор
  not not_1 (not_1_out, \menu_1_пауза_игра );
  or or_3 (or_3_out, comparator_5_eq, comparator_6_eq);
  or or_4 (or_4_out, comparator_7_eq, comparator_8_eq);
  and and_1 (and_1_out, not_1_out, \menu_1_меню_игра );
  J_K_Flip_Flop j_k_ff_3 (
    .J(or_3_out), .clk(or_3_out), .K(or_3_out), .Q(upRp), .Qn(j_k_ff_3_qn), .reset(counter_3_q[1]));  // open: preset, en
  J_K_Flip_Flop j_k_ff_4 (
    .J(or_4_out), .clk(or_4_out), .K(or_4_out), .Q(downRp), .Qn(j_k_ff_4_qn), .reset(counter_4_q[1]));  // open: preset, en
  x x_1 (.reset(restart), .out_2(x1), .hit(hit), .vel_X(vel_X), .out(x2), .\игра (and_1_out));
  Counter #(.width(2), .max('h3)) counter_3 (
    .count(upRp), .Q(counter_3_q), .clk(clock_1_out), .clr(j_k_ff_3_qn));  // open: load, D, carry
  Counter #(.width(2), .max('h3)) counter_4 (
    .count(downRp), .Q(counter_4_q), .clk(clock_1_out), .clr(j_k_ff_4_qn));  // open: load, D, carry
  Multiplexer multiplexer_1 (.in0(comparator_9_gt), .in1(upRp), .out(multiplexer_1_out), .sel(_1_2p));  // open: en
  y y_1 (.hit(hit), .reset(restart), .out(y), .vel_Y(vel_Y), .\игра (and_1_out));
  temp temp_1 (
    .upL(upL), .downL(downL), .\рядом_слева (\рядом_слева ), .y(y), .\рядом_справа (\рядом_справа ),
    .outR(out_R), .hit(hit), .outL(out_L), .reset(restart), .upR(multiplexer_1_out), .downR(multiplexer_2_out));
  Multiplexer multiplexer_2 (.in0(comparator_9_lt), .in1(downRp), .out(multiplexer_2_out), .sel(_1_2p));  // open: en
  Comparator #(.width(32)) comparator_9 (
    .a(botres), .b(out_R), .gt(comparator_9_gt), .lt(comparator_9_lt));  // open: eq

  // Other names for the same wires on the sheet: reset = restart

  // Notes on the sheet:
  //   w
  //   W
  //   s
  //   S
  //   i
  //   I
  //   k
  //   K
endmodule
